// Logisim project ep221.circ as structural Verilog: 15 circuits, main circuit EP2
module EP2 (
  input  in_1,
  input  in_2,
  input  in_3,
  input  in_4,
  input  in_5,
  input  in_6,
  input  in_7,
  input  in_8,
  input  in_9,
  input  in_10,
  input  in_11,
  input  in_12,
  input  in_13,
  input  in_14,
  input  in_15,
  input  in_16,
  input  in_17,
  input  in_18,
  input  Subtrator_A___B
);

  wire alu_1_out_5;
  wire [3:0] alu_1_out_4;
  wire [7:4] alu_1_out_4_2;

  Hex_Digit_Display hex_digit_display_1 (.value({in_9, in_10, in_11, in_12}));  // open: dp
  Hex_Digit_Display hex_digit_display_2 (.value(alu_1_out_4));  // open: dp
  Hex_Digit_Display hex_digit_display_3 (.value(alu_1_out_4_2));  // open: dp
  Hex_Digit_Display hex_digit_display_4 (.value({in_13, in_14, in_15, in_16}));  // open: dp
  LED led_1 (.in(alu_1_out_4_2[7]));
  LED led_2 (.in(alu_1_out_4_2[5]));
  LED led_3 (.in(alu_1_out_4_2[6]));
  LED led_4 (.in(alu_1_out_4_2[4]));
  LED led_5 (.in(alu_1_out_4[3]));
  LED led_6 (.in(alu_1_out_4[2]));
  LED led_7 (.in(alu_1_out_4[1]));
  LED led_8 (.in(alu_1_out_4[0]));
  ALU alu_1 (
    .in_2({in_9, in_10, in_11, in_12, in_13, in_14, in_15, in_16}), .in_3({in_17, in_18, Subtrator_A___B}),
    .in_1({in_1, in_2, in_3, in_4, in_5, in_6, in_7, in_8}), .out_4({alu_1_out_4_2, alu_1_out_4}),
    .out_5(alu_1_out_5));
  LED Overflow (.in(alu_1_out_5));
  Hex_Digit_Display hex_digit_display_5 (.value({in_1, in_2, in_3, in_4}));  // open: dp
  Hex_Digit_Display hex_digit_display_6 (.value({in_5, in_6, in_7, in_8}));  // open: dp

  // Notes on the sheet:
  //   B
  //   a+b
  //   de -127 até 128 = 256 num
  //   8-bit Adder - Hexadecimal Representation
  //   Overflow multiplicação?!
  //   alterar o terra para constante zero
  //   A
endmodule

module _8_bit_Riple_Carry_Adder (
  input  [7:0] in_1,
  input  [7:0] in_2,
  input  OP_Code,
  input  Carry_Inicial,
  output overflow,
  output [7:0] out_6
);

  wire complemento_de_dois_1_out, complemento_de_dois_1_out_2, complemento_de_dois_1_out_3,
       complemento_de_dois_1_out_4, complemento_de_dois_1_out_5, complemento_de_dois_1_out_6,
       complemento_de_dois_1_out_7, complemento_de_dois_1_out_8, full_adder_1_answer_bit,
       full_adder_1_carry_bit, full_adder_2_answer_bit, full_adder_2_carry_bit, full_adder_3_answer_bit,
       full_adder_3_carry_bit, full_adder_4_answer_bit, full_adder_4_carry_bit, full_adder_5_answer_bit,
       full_adder_5_carry_bit, full_adder_6_answer_bit, full_adder_6_carry_bit, full_adder_7_answer_bit,
       full_adder_7_carry_bit, full_adder_8_answer_bit, full_adder_8_carry_bit, not_1_out;

  not not_1 (not_1_out, OP_Code);
  and and_1 (overflow, not_1_out, full_adder_1_carry_bit);
  Full_Adder full_adder_1 (
    .a(in_2[7]), .b(complemento_de_dois_1_out_2), .c__carry(full_adder_2_carry_bit),
    .Carry_Bit(full_adder_1_carry_bit), .Answer_Bit(full_adder_1_answer_bit));
  Full_Adder full_adder_2 (
    .a(in_2[6]), .b(complemento_de_dois_1_out), .c__carry(full_adder_3_carry_bit),
    .Carry_Bit(full_adder_2_carry_bit), .Answer_Bit(full_adder_2_answer_bit));
  complemento_de_dois complemento_de_dois_1 (
    .OP_Code(OP_Code), .B(in_1[7]), .B_2(in_1[6]), .B_3(in_1[5]), .B_4(in_1[4]), .B_5(in_1[3]),
    .B_6(in_1[2]), .B_7(in_1[1]), .B_8(in_1[0]), .Out_2(complemento_de_dois_1_out_2),
    .Out_3(complemento_de_dois_1_out_3), .Out_5(complemento_de_dois_1_out_5),
    .Out_7(complemento_de_dois_1_out_7), .Out_8(complemento_de_dois_1_out_8),
    .Out(complemento_de_dois_1_out), .Out_6(complemento_de_dois_1_out_6), .Out_4(complemento_de_dois_1_out_4));
  Adder1 adder1_1 (
    .Comp_2(OP_Code), .O7(full_adder_1_answer_bit), .O6(full_adder_2_answer_bit),
    .O5(full_adder_3_answer_bit), .O4(full_adder_4_answer_bit), .O3(full_adder_5_answer_bit),
    .O2(full_adder_6_answer_bit), .O1(full_adder_7_answer_bit), .O0(full_adder_8_answer_bit),
    .out_10(out_6[7]), .out_11(out_6[6]), .out_12(out_6[5]), .out_13(out_6[4]), .out_14(out_6[3]),
    .out_15(out_6[2]), .out_16(out_6[1]), .out_17(out_6[0]));
  Full_Adder full_adder_3 (
    .a(in_2[5]), .b(complemento_de_dois_1_out_3), .c__carry(full_adder_4_carry_bit),
    .Carry_Bit(full_adder_3_carry_bit), .Answer_Bit(full_adder_3_answer_bit));
  Full_Adder full_adder_4 (
    .a(in_2[4]), .b(complemento_de_dois_1_out_4), .c__carry(full_adder_5_carry_bit),
    .Carry_Bit(full_adder_4_carry_bit), .Answer_Bit(full_adder_4_answer_bit));
  Full_Adder full_adder_5 (
    .a(in_2[3]), .b(complemento_de_dois_1_out_5), .c__carry(full_adder_6_carry_bit),
    .Carry_Bit(full_adder_5_carry_bit), .Answer_Bit(full_adder_5_answer_bit));
  Full_Adder full_adder_6 (
    .a(in_2[2]), .b(complemento_de_dois_1_out_6), .c__carry(full_adder_7_carry_bit),
    .Carry_Bit(full_adder_6_carry_bit), .Answer_Bit(full_adder_6_answer_bit));
  Full_Adder full_adder_7 (
    .a(in_2[1]), .b(complemento_de_dois_1_out_7), .c__carry(full_adder_8_carry_bit),
    .Carry_Bit(full_adder_7_carry_bit), .Answer_Bit(full_adder_7_answer_bit));
  Full_Adder full_adder_8 (
    .a(in_2[0]), .b(complemento_de_dois_1_out_8), .c__carry(Carry_Inicial),
    .Carry_Bit(full_adder_8_carry_bit), .Answer_Bit(full_adder_8_answer_bit));
endmodule

module Full_Adder (
  input  a,
  input  b,
  input  c__carry,
  output Answer_Bit,
  output Carry_Bit
);

  wire and_1_out, and_2_out, and_3_out, xor_1_out;

  xor xor_1 (xor_1_out, b, c__carry);
  xor xor_2 (Answer_Bit, a, xor_1_out);
  and and_1 (and_1_out, b, c__carry);
  and and_2 (and_2_out, b, a);
  and and_3 (and_3_out, c__carry, a);
  or or_1 (Carry_Bit, and_1_out, and_2_out, and_3_out);
endmodule

module complemento_de_dois (
  input  B,
  input  B_2,
  input  B_3,
  input  B_4,
  input  B_5,
  input  B_6,
  input  B_7,
  input  B_8,
  input  OP_Code,
  output Out,
  output Out_2,
  output Out_3,
  output Out_4,
  output Out_5,
  output Out_6,
  output Out_7,
  output Out_8
);

  xor xor_1 (Out, B, OP_Code);
  xor xor_2 (Out_2, B_2, OP_Code);
  xor xor_3 (Out_3, B_3, OP_Code);
  xor xor_4 (Out_4, B_4, OP_Code);
  xor xor_5 (Out_5, B_5, OP_Code);
  xor xor_6 (Out_6, B_6, OP_Code);
  xor xor_7 (Out_7, B_7, OP_Code);
  xor xor_8 (Out_8, B_8, OP_Code);
endmodule

module Adder1 (
  input  Comp_2,
  input  O7,
  input  O6,
  input  O5,
  input  O4,
  input  O3,
  input  O2,
  input  O1,
  input  O0,
  output out_10,
  output out_11,
  output out_12,
  output out_13,
  output out_14,
  output out_15,
  output out_16,
  output out_17
);

  wire full_adder_1_carry_bit, full_adder_2_carry_bit, full_adder_3_carry_bit, full_adder_4_carry_bit,
       full_adder_5_carry_bit, full_adder_6_carry_bit, full_adder_7_carry_bit, full_adder_8_carry_bit;

  LED led_1 (.in(full_adder_1_carry_bit));
  Full_Adder full_adder_1 (
    .a(O7), .b(1'b0), .c__carry(full_adder_2_carry_bit), .Carry_Bit(full_adder_1_carry_bit),
    .Answer_Bit(out_10));
  Full_Adder full_adder_2 (
    .a(O6), .b(1'b0), .c__carry(full_adder_3_carry_bit), .Carry_Bit(full_adder_2_carry_bit),
    .Answer_Bit(out_11));
  Full_Adder full_adder_3 (
    .a(O5), .b(1'b0), .c__carry(full_adder_4_carry_bit), .Carry_Bit(full_adder_3_carry_bit),
    .Answer_Bit(out_12));
  Full_Adder full_adder_4 (
    .a(O4), .b(1'b0), .c__carry(full_adder_5_carry_bit), .Carry_Bit(full_adder_4_carry_bit),
    .Answer_Bit(out_13));
  Full_Adder full_adder_5 (
    .a(O3), .b(1'b0), .c__carry(full_adder_6_carry_bit), .Carry_Bit(full_adder_5_carry_bit),
    .Answer_Bit(out_14));
  Full_Adder full_adder_6 (
    .a(O2), .b(1'b0), .c__carry(full_adder_7_carry_bit), .Carry_Bit(full_adder_6_carry_bit),
    .Answer_Bit(out_15));
  Full_Adder full_adder_7 (
    .a(O1), .b(1'b0), .c__carry(full_adder_8_carry_bit), .Carry_Bit(full_adder_7_carry_bit),
    .Answer_Bit(out_16));
  Full_Adder full_adder_8 (
    .a(O0), .b(Comp_2), .c__carry(1'b0), .Carry_Bit(full_adder_8_carry_bit), .Answer_Bit(out_17));
endmodule

module multi (
  input  B7,
  input  B6,
  input  B5,
  input  B4,
  input  [7:0] in_5,
  input  B3,
  input  B2,
  input  B1,
  input  B0,
  input  in_10,
  output [7:0] out_11
);

  wire adder_usado_na_multiplicacao_1_overflow, adder_usado_na_multiplicacao_2_overflow,
       adder_usado_na_multiplicacao_3_overflow, adder_usado_na_multiplicacao_4_overflow,
       adder_usado_na_multiplicacao_5_overflow, adder_usado_na_multiplicacao_6_overflow,
       adder_usado_na_multiplicacao_7_overflow, and_2_out_10, and_2_out_11, and_2_out_12, and_2_out_13,
       and_2_out_14, and_2_out_15, and_2_out_16, and_2_out_17, and_3_out_10, and_3_out_11, and_3_out_12,
       and_3_out_13, and_3_out_14, and_3_out_15, and_3_out_16, and_3_out_17, and_4_out_10, and_4_out_11,
       and_4_out_12, and_4_out_13, and_4_out_14, and_4_out_15, and_4_out_16, and_4_out_17, and_5_out_10,
       and_5_out_11, and_5_out_12, and_5_out_13, and_5_out_14, and_5_out_15, and_5_out_16, and_5_out_17,
       and_6_out_10, and_6_out_11, and_6_out_12, and_6_out_13, and_6_out_14, and_6_out_15, and_6_out_16,
       and_6_out_17, and_7_out_10, and_7_out_11, and_7_out_12, and_7_out_13, and_7_out_14, and_7_out_15,
       and_7_out_16, and_7_out_17, and_8_out_10, and_8_out_11, and_8_out_12, and_8_out_13, and_8_out_14,
       and_8_out_15, and_8_out_16, and_8_out_17, right_shift_3_out_9, right_shift_3_out_10,
       right_shift_3_out_11, right_shift_3_out_12, right_shift_3_out_13, right_shift_3_out_14,
       right_shift_3_out_15, right_shift_3_out_16, right_shift_5_out_9, right_shift_5_out_10,
       right_shift_5_out_11, right_shift_5_out_12, right_shift_5_out_13, right_shift_5_out_14,
       right_shift_5_out_15, right_shift_5_out_16, right_shift_6_out_9, right_shift_6_out_10,
       right_shift_6_out_11, right_shift_6_out_12, right_shift_6_out_13, right_shift_6_out_14,
       right_shift_6_out_15, right_shift_6_out_16, right_shift_7_out_9, right_shift_7_out_10,
       right_shift_7_out_11, right_shift_7_out_12, right_shift_7_out_13, right_shift_7_out_14,
       right_shift_7_out_15, right_shift_7_out_16, right_shift_8_out_9, right_shift_8_out_10,
       right_shift_8_out_11, right_shift_8_out_12, right_shift_8_out_13, right_shift_8_out_14,
       right_shift_8_out_15, right_shift_8_out_16, right_shift_9_out_9, right_shift_9_out_10,
       right_shift_9_out_11, right_shift_9_out_12, right_shift_9_out_13, right_shift_9_out_14,
       right_shift_9_out_15, right_shift_9_out_16, right_shift_10_out_9, right_shift_10_out_10,
       right_shift_10_out_11, right_shift_10_out_12, right_shift_10_out_13, right_shift_10_out_14,
       right_shift_10_out_15, right_shift_10_out_16, right_shift_12_out_9, right_shift_12_out_10,
       right_shift_12_out_11, right_shift_12_out_12, right_shift_12_out_13, right_shift_12_out_14,
       right_shift_12_out_15, right_shift_12_out_16, right_shift_13_out_9, right_shift_13_out_10,
       right_shift_13_out_11, right_shift_13_out_12, right_shift_13_out_13, right_shift_13_out_14,
       right_shift_13_out_15, right_shift_13_out_16, right_shift_14_out_9, right_shift_14_out_10,
       right_shift_14_out_11, right_shift_14_out_12, right_shift_14_out_13, right_shift_14_out_14,
       right_shift_14_out_15, right_shift_14_out_16, right_shift_15_out_9, right_shift_15_out_10,
       right_shift_15_out_11, right_shift_15_out_12, right_shift_15_out_13, right_shift_15_out_14,
       right_shift_15_out_15, right_shift_15_out_16, right_shift_16_out_9, right_shift_16_out_10,
       right_shift_16_out_11, right_shift_16_out_12, right_shift_16_out_13, right_shift_16_out_14,
       right_shift_16_out_15, right_shift_16_out_16, right_shift_18_out_9, right_shift_18_out_10,
       right_shift_18_out_11, right_shift_18_out_12, right_shift_18_out_13, right_shift_18_out_14,
       right_shift_18_out_15, right_shift_18_out_16, right_shift_19_out_9, right_shift_19_out_10,
       right_shift_19_out_11, right_shift_19_out_12, right_shift_19_out_13, right_shift_19_out_14,
       right_shift_19_out_15, right_shift_19_out_16, right_shift_20_out_9, right_shift_20_out_10,
       right_shift_20_out_11, right_shift_20_out_12, right_shift_20_out_13, right_shift_20_out_14,
       right_shift_20_out_15, right_shift_20_out_16, right_shift_21_out_9, right_shift_21_out_10,
       right_shift_21_out_11, right_shift_21_out_12, right_shift_21_out_13, right_shift_21_out_14,
       right_shift_21_out_15, right_shift_21_out_16, right_shift_22_out_9, right_shift_22_out_10,
       right_shift_22_out_11, right_shift_22_out_12, right_shift_22_out_13, right_shift_22_out_14,
       right_shift_22_out_15, right_shift_22_out_16, right_shift_23_out_9, right_shift_23_out_10,
       right_shift_23_out_11, right_shift_23_out_12, right_shift_23_out_13, right_shift_23_out_14,
       right_shift_23_out_15, right_shift_23_out_16, right_shift_24_out_9, right_shift_24_out_10,
       right_shift_24_out_11, right_shift_24_out_12, right_shift_24_out_13, right_shift_24_out_14,
       right_shift_24_out_15, right_shift_24_out_16, right_shift_26_out_9, right_shift_26_out_10,
       right_shift_26_out_11, right_shift_26_out_12, right_shift_26_out_13, right_shift_26_out_14,
       right_shift_26_out_15, right_shift_26_out_16, right_shift_28_out_9, right_shift_28_out_10,
       right_shift_28_out_11, right_shift_28_out_12, right_shift_28_out_13, right_shift_28_out_14,
       right_shift_28_out_15, right_shift_28_out_16;
  wire [7:0] adder_usado_na_multiplicacao_1_out_4, adder_usado_na_multiplicacao_2_out_4,
       adder_usado_na_multiplicacao_3_out_4, adder_usado_na_multiplicacao_4_out_4,
       adder_usado_na_multiplicacao_5_out_4, adder_usado_na_multiplicacao_6_out_4, and_1_out_10,
       right_shift_1_out_9, right_shift_2_out_9, right_shift_4_out_9, right_shift_11_out_9,
       right_shift_17_out_9, right_shift_25_out_9, right_shift_27_out_9;

  And and_1 (
    .in_1(in_5[0]), .in_2(in_5[1]), .in_3(in_5[2]), .in_4(in_5[3]), .in_5(in_5[4]), .in_6(in_5[5]),
    .in_7(in_5[6]), .in_8(in_5[7]), .in_9(B0), .out_10(and_1_out_10[0]), .out_11(and_1_out_10[1]),
    .out_12(and_1_out_10[2]), .out_13(and_1_out_10[3]), .out_14(and_1_out_10[4]), .out_15(and_1_out_10[5]),
    .out_16(and_1_out_10[6]), .out_17(and_1_out_10[7]));
  Adder_usado_na_multiplicacao adder_usado_na_multiplicacao_1 (
    .in_1(right_shift_1_out_9), .in_2(and_1_out_10), .overflow(adder_usado_na_multiplicacao_1_overflow),
    .out_4(adder_usado_na_multiplicacao_1_out_4));
  And and_2 (
    .in_1(in_5[0]), .in_2(in_5[1]), .in_3(in_5[2]), .in_4(in_5[3]), .in_5(in_5[4]), .in_6(in_5[5]),
    .in_7(in_5[6]), .in_8(in_5[7]), .in_9(B1), .out_10(and_2_out_10), .out_11(and_2_out_11),
    .out_12(and_2_out_12), .out_13(and_2_out_13), .out_14(and_2_out_14), .out_15(and_2_out_15),
    .out_16(and_2_out_16), .out_17(and_2_out_17));
  And and_3 (
    .in_1(in_5[0]), .in_2(in_5[1]), .in_3(in_5[2]), .in_4(in_5[3]), .in_5(in_5[4]), .in_6(in_5[5]),
    .in_7(in_5[6]), .in_8(in_5[7]), .in_9(B2), .out_10(and_3_out_10), .out_11(and_3_out_11),
    .out_12(and_3_out_12), .out_13(and_3_out_13), .out_14(and_3_out_14), .out_15(and_3_out_15),
    .out_16(and_3_out_16), .out_17(and_3_out_17));
  right_shift right_shift_1 (
    .in_1(and_2_out_10), .in_2(and_2_out_11), .in_3(and_2_out_12), .in_4(and_2_out_13), .in_5(and_2_out_14),
    .in_6(and_2_out_15), .in_7(and_2_out_16), .in_8(and_2_out_17), .out_9(right_shift_1_out_9[0]),
    .out_10(right_shift_1_out_9[1]), .out_11(right_shift_1_out_9[2]), .out_12(right_shift_1_out_9[3]),
    .out_13(right_shift_1_out_9[4]), .out_14(right_shift_1_out_9[5]), .out_15(right_shift_1_out_9[6]),
    .out_16(right_shift_1_out_9[7]));
  And and_4 (
    .in_1(in_5[0]), .in_2(in_5[1]), .in_3(in_5[2]), .in_4(in_5[3]), .in_5(in_5[4]), .in_6(in_5[5]),
    .in_7(in_5[6]), .in_8(in_5[7]), .in_9(B3), .out_10(and_4_out_10), .out_11(and_4_out_11),
    .out_12(and_4_out_12), .out_13(and_4_out_13), .out_14(and_4_out_14), .out_15(and_4_out_15),
    .out_16(and_4_out_16), .out_17(and_4_out_17));
  right_shift right_shift_2 (
    .in_1(right_shift_3_out_9), .in_2(right_shift_3_out_10), .in_3(right_shift_3_out_11),
    .in_4(right_shift_3_out_12), .in_5(right_shift_3_out_13), .in_6(right_shift_3_out_14),
    .in_7(right_shift_3_out_15), .in_8(right_shift_3_out_16), .out_9(right_shift_2_out_9[0]),
    .out_10(right_shift_2_out_9[1]), .out_11(right_shift_2_out_9[2]), .out_12(right_shift_2_out_9[3]),
    .out_13(right_shift_2_out_9[4]), .out_14(right_shift_2_out_9[5]), .out_15(right_shift_2_out_9[6]),
    .out_16(right_shift_2_out_9[7]));
  right_shift right_shift_3 (
    .in_1(and_3_out_10), .in_2(and_3_out_11), .in_3(and_3_out_12), .in_4(and_3_out_13), .in_5(and_3_out_14),
    .in_6(and_3_out_15), .in_7(and_3_out_16), .in_8(and_3_out_17), .out_9(right_shift_3_out_9),
    .out_10(right_shift_3_out_10), .out_11(right_shift_3_out_11), .out_12(right_shift_3_out_12),
    .out_13(right_shift_3_out_13), .out_14(right_shift_3_out_14), .out_15(right_shift_3_out_15),
    .out_16(right_shift_3_out_16));
  Adder_usado_na_multiplicacao adder_usado_na_multiplicacao_2 (
    .in_1(right_shift_2_out_9), .in_2(adder_usado_na_multiplicacao_1_out_4),
    .overflow(adder_usado_na_multiplicacao_2_overflow), .out_4(adder_usado_na_multiplicacao_2_out_4));
  And and_5 (
    .in_1(in_5[0]), .in_2(in_5[1]), .in_3(in_5[2]), .in_4(in_5[3]), .in_5(in_5[4]), .in_6(in_5[5]),
    .in_7(in_5[6]), .in_8(in_5[7]), .in_9(B4), .out_10(and_5_out_10), .out_11(and_5_out_11),
    .out_12(and_5_out_12), .out_13(and_5_out_13), .out_14(and_5_out_14), .out_15(and_5_out_15),
    .out_16(and_5_out_16), .out_17(and_5_out_17));
  right_shift right_shift_4 (
    .in_1(right_shift_6_out_9), .in_2(right_shift_6_out_10), .in_3(right_shift_6_out_11),
    .in_4(right_shift_6_out_12), .in_5(right_shift_6_out_13), .in_6(right_shift_6_out_14),
    .in_7(right_shift_6_out_15), .in_8(right_shift_6_out_16), .out_9(right_shift_4_out_9[0]),
    .out_10(right_shift_4_out_9[1]), .out_11(right_shift_4_out_9[2]), .out_12(right_shift_4_out_9[3]),
    .out_13(right_shift_4_out_9[4]), .out_14(right_shift_4_out_9[5]), .out_15(right_shift_4_out_9[6]),
    .out_16(right_shift_4_out_9[7]));
  right_shift right_shift_5 (
    .in_1(and_4_out_10), .in_2(and_4_out_11), .in_3(and_4_out_12), .in_4(and_4_out_13), .in_5(and_4_out_14),
    .in_6(and_4_out_15), .in_7(and_4_out_16), .in_8(and_4_out_17), .out_9(right_shift_5_out_9),
    .out_10(right_shift_5_out_10), .out_11(right_shift_5_out_11), .out_12(right_shift_5_out_12),
    .out_13(right_shift_5_out_13), .out_14(right_shift_5_out_14), .out_15(right_shift_5_out_15),
    .out_16(right_shift_5_out_16));
  right_shift right_shift_6 (
    .in_1(right_shift_5_out_9), .in_2(right_shift_5_out_10), .in_3(right_shift_5_out_11),
    .in_4(right_shift_5_out_12), .in_5(right_shift_5_out_13), .in_6(right_shift_5_out_14),
    .in_7(right_shift_5_out_15), .in_8(right_shift_5_out_16), .out_9(right_shift_6_out_9),
    .out_10(right_shift_6_out_10), .out_11(right_shift_6_out_11), .out_12(right_shift_6_out_12),
    .out_13(right_shift_6_out_13), .out_14(right_shift_6_out_14), .out_15(right_shift_6_out_15),
    .out_16(right_shift_6_out_16));
  right_shift right_shift_7 (
    .in_1(right_shift_8_out_9), .in_2(right_shift_8_out_10), .in_3(right_shift_8_out_11),
    .in_4(right_shift_8_out_12), .in_5(right_shift_8_out_13), .in_6(right_shift_8_out_14),
    .in_7(right_shift_8_out_15), .in_8(right_shift_8_out_16), .out_9(right_shift_7_out_9),
    .out_10(right_shift_7_out_10), .out_11(right_shift_7_out_11), .out_12(right_shift_7_out_12),
    .out_13(right_shift_7_out_13), .out_14(right_shift_7_out_14), .out_15(right_shift_7_out_15),
    .out_16(right_shift_7_out_16));
  right_shift right_shift_8 (
    .in_1(and_5_out_10), .in_2(and_5_out_11), .in_3(and_5_out_12), .in_4(and_5_out_13), .in_5(and_5_out_14),
    .in_6(and_5_out_15), .in_7(and_5_out_16), .in_8(and_5_out_17), .out_9(right_shift_8_out_9),
    .out_10(right_shift_8_out_10), .out_11(right_shift_8_out_11), .out_12(right_shift_8_out_12),
    .out_13(right_shift_8_out_13), .out_14(right_shift_8_out_14), .out_15(right_shift_8_out_15),
    .out_16(right_shift_8_out_16));
  right_shift right_shift_9 (
    .in_1(right_shift_7_out_9), .in_2(right_shift_7_out_10), .in_3(right_shift_7_out_11),
    .in_4(right_shift_7_out_12), .in_5(right_shift_7_out_13), .in_6(right_shift_7_out_14),
    .in_7(right_shift_7_out_15), .in_8(right_shift_7_out_16), .out_9(right_shift_9_out_9),
    .out_10(right_shift_9_out_10), .out_11(right_shift_9_out_11), .out_12(right_shift_9_out_12),
    .out_13(right_shift_9_out_13), .out_14(right_shift_9_out_14), .out_15(right_shift_9_out_15),
    .out_16(right_shift_9_out_16));
  Adder_usado_na_multiplicacao adder_usado_na_multiplicacao_3 (
    .in_1(right_shift_4_out_9), .in_2(adder_usado_na_multiplicacao_2_out_4),
    .overflow(adder_usado_na_multiplicacao_3_overflow), .out_4(adder_usado_na_multiplicacao_3_out_4));
  And and_6 (
    .in_1(in_5[0]), .in_2(in_5[1]), .in_3(in_5[2]), .in_4(in_5[3]), .in_5(in_5[4]), .in_6(in_5[5]),
    .in_7(in_5[6]), .in_8(in_5[7]), .in_9(B5), .out_10(and_6_out_10), .out_11(and_6_out_11),
    .out_12(and_6_out_12), .out_13(and_6_out_13), .out_14(and_6_out_14), .out_15(and_6_out_15),
    .out_16(and_6_out_16), .out_17(and_6_out_17));
  right_shift right_shift_10 (
    .in_1(and_6_out_10), .in_2(and_6_out_11), .in_3(and_6_out_12), .in_4(and_6_out_13), .in_5(and_6_out_14),
    .in_6(and_6_out_15), .in_7(and_6_out_16), .in_8(and_6_out_17), .out_9(right_shift_10_out_9),
    .out_10(right_shift_10_out_10), .out_11(right_shift_10_out_11), .out_12(right_shift_10_out_12),
    .out_13(right_shift_10_out_13), .out_14(right_shift_10_out_14), .out_15(right_shift_10_out_15),
    .out_16(right_shift_10_out_16));
  right_shift right_shift_11 (
    .in_1(right_shift_9_out_9), .in_2(right_shift_9_out_10), .in_3(right_shift_9_out_11),
    .in_4(right_shift_9_out_12), .in_5(right_shift_9_out_13), .in_6(right_shift_9_out_14),
    .in_7(right_shift_9_out_15), .in_8(right_shift_9_out_16), .out_9(right_shift_11_out_9[0]),
    .out_10(right_shift_11_out_9[1]), .out_11(right_shift_11_out_9[2]), .out_12(right_shift_11_out_9[3]),
    .out_13(right_shift_11_out_9[4]), .out_14(right_shift_11_out_9[5]), .out_15(right_shift_11_out_9[6]),
    .out_16(right_shift_11_out_9[7]));
  Adder_usado_na_multiplicacao adder_usado_na_multiplicacao_4 (
    .in_1(right_shift_11_out_9), .in_2(adder_usado_na_multiplicacao_3_out_4),
    .overflow(adder_usado_na_multiplicacao_4_overflow), .out_4(adder_usado_na_multiplicacao_4_out_4));
  right_shift right_shift_12 (
    .in_1(right_shift_13_out_9), .in_2(right_shift_13_out_10), .in_3(right_shift_13_out_11),
    .in_4(right_shift_13_out_12), .in_5(right_shift_13_out_13), .in_6(right_shift_13_out_14),
    .in_7(right_shift_13_out_15), .in_8(right_shift_13_out_16), .out_9(right_shift_12_out_9),
    .out_10(right_shift_12_out_10), .out_11(right_shift_12_out_11), .out_12(right_shift_12_out_12),
    .out_13(right_shift_12_out_13), .out_14(right_shift_12_out_14), .out_15(right_shift_12_out_15),
    .out_16(right_shift_12_out_16));
  right_shift right_shift_13 (
    .in_1(right_shift_10_out_9), .in_2(right_shift_10_out_10), .in_3(right_shift_10_out_11),
    .in_4(right_shift_10_out_12), .in_5(right_shift_10_out_13), .in_6(right_shift_10_out_14),
    .in_7(right_shift_10_out_15), .in_8(right_shift_10_out_16), .out_9(right_shift_13_out_9),
    .out_10(right_shift_13_out_10), .out_11(right_shift_13_out_11), .out_12(right_shift_13_out_12),
    .out_13(right_shift_13_out_13), .out_14(right_shift_13_out_14), .out_15(right_shift_13_out_15),
    .out_16(right_shift_13_out_16));
  right_shift right_shift_14 (
    .in_1(right_shift_15_out_9), .in_2(right_shift_15_out_10), .in_3(right_shift_15_out_11),
    .in_4(right_shift_15_out_12), .in_5(right_shift_15_out_13), .in_6(right_shift_15_out_14),
    .in_7(right_shift_15_out_15), .in_8(right_shift_15_out_16), .out_9(right_shift_14_out_9),
    .out_10(right_shift_14_out_10), .out_11(right_shift_14_out_11), .out_12(right_shift_14_out_12),
    .out_13(right_shift_14_out_13), .out_14(right_shift_14_out_14), .out_15(right_shift_14_out_15),
    .out_16(right_shift_14_out_16));
  right_shift right_shift_15 (
    .in_1(and_7_out_10), .in_2(and_7_out_11), .in_3(and_7_out_12), .in_4(and_7_out_13), .in_5(and_7_out_14),
    .in_6(and_7_out_15), .in_7(and_7_out_16), .in_8(and_7_out_17), .out_9(right_shift_15_out_9),
    .out_10(right_shift_15_out_10), .out_11(right_shift_15_out_11), .out_12(right_shift_15_out_12),
    .out_13(right_shift_15_out_13), .out_14(right_shift_15_out_14), .out_15(right_shift_15_out_15),
    .out_16(right_shift_15_out_16));
  And and_7 (
    .in_1(in_5[0]), .in_2(in_5[1]), .in_3(in_5[2]), .in_4(in_5[3]), .in_5(in_5[4]), .in_6(in_5[5]),
    .in_7(in_5[6]), .in_8(in_5[7]), .in_9(B6), .out_10(and_7_out_10), .out_11(and_7_out_11),
    .out_12(and_7_out_12), .out_13(and_7_out_13), .out_14(and_7_out_14), .out_15(and_7_out_15),
    .out_16(and_7_out_16), .out_17(and_7_out_17));
  right_shift right_shift_16 (
    .in_1(right_shift_12_out_9), .in_2(right_shift_12_out_10), .in_3(right_shift_12_out_11),
    .in_4(right_shift_12_out_12), .in_5(right_shift_12_out_13), .in_6(right_shift_12_out_14),
    .in_7(right_shift_12_out_15), .in_8(right_shift_12_out_16), .out_9(right_shift_16_out_9),
    .out_10(right_shift_16_out_10), .out_11(right_shift_16_out_11), .out_12(right_shift_16_out_12),
    .out_13(right_shift_16_out_13), .out_14(right_shift_16_out_14), .out_15(right_shift_16_out_15),
    .out_16(right_shift_16_out_16));
  right_shift right_shift_17 (
    .in_1(right_shift_16_out_9), .in_2(right_shift_16_out_10), .in_3(right_shift_16_out_11),
    .in_4(right_shift_16_out_12), .in_5(right_shift_16_out_13), .in_6(right_shift_16_out_14),
    .in_7(right_shift_16_out_15), .in_8(right_shift_16_out_16), .out_9(right_shift_17_out_9[0]),
    .out_10(right_shift_17_out_9[1]), .out_11(right_shift_17_out_9[2]), .out_12(right_shift_17_out_9[3]),
    .out_13(right_shift_17_out_9[4]), .out_14(right_shift_17_out_9[5]), .out_15(right_shift_17_out_9[6]),
    .out_16(right_shift_17_out_9[7]));
  Adder_usado_na_multiplicacao adder_usado_na_multiplicacao_5 (
    .in_1(right_shift_17_out_9), .in_2(adder_usado_na_multiplicacao_4_out_4),
    .overflow(adder_usado_na_multiplicacao_5_overflow), .out_4(adder_usado_na_multiplicacao_5_out_4));
  right_shift right_shift_18 (
    .in_1(right_shift_19_out_9), .in_2(right_shift_19_out_10), .in_3(right_shift_19_out_11),
    .in_4(right_shift_19_out_12), .in_5(right_shift_19_out_13), .in_6(right_shift_19_out_14),
    .in_7(right_shift_19_out_15), .in_8(right_shift_19_out_16), .out_9(right_shift_18_out_9),
    .out_10(right_shift_18_out_10), .out_11(right_shift_18_out_11), .out_12(right_shift_18_out_12),
    .out_13(right_shift_18_out_13), .out_14(right_shift_18_out_14), .out_15(right_shift_18_out_15),
    .out_16(right_shift_18_out_16));
  right_shift right_shift_19 (
    .in_1(and_8_out_10), .in_2(and_8_out_11), .in_3(and_8_out_12), .in_4(and_8_out_13), .in_5(and_8_out_14),
    .in_6(and_8_out_15), .in_7(and_8_out_16), .in_8(and_8_out_17), .out_9(right_shift_19_out_9),
    .out_10(right_shift_19_out_10), .out_11(right_shift_19_out_11), .out_12(right_shift_19_out_12),
    .out_13(right_shift_19_out_13), .out_14(right_shift_19_out_14), .out_15(right_shift_19_out_15),
    .out_16(right_shift_19_out_16));
  And and_8 (
    .in_1(in_5[0]), .in_2(in_5[1]), .in_3(in_5[2]), .in_4(in_5[3]), .in_5(in_5[4]), .in_6(in_5[5]),
    .in_7(in_5[6]), .in_8(in_5[7]), .in_9(B7), .out_10(and_8_out_10), .out_11(and_8_out_11),
    .out_12(and_8_out_12), .out_13(and_8_out_13), .out_14(and_8_out_14), .out_15(and_8_out_15),
    .out_16(and_8_out_16), .out_17(and_8_out_17));
  right_shift right_shift_20 (
    .in_1(right_shift_21_out_9), .in_2(right_shift_21_out_10), .in_3(right_shift_21_out_11),
    .in_4(right_shift_21_out_12), .in_5(right_shift_21_out_13), .in_6(right_shift_21_out_14),
    .in_7(right_shift_21_out_15), .in_8(right_shift_21_out_16), .out_9(right_shift_20_out_9),
    .out_10(right_shift_20_out_10), .out_11(right_shift_20_out_11), .out_12(right_shift_20_out_12),
    .out_13(right_shift_20_out_13), .out_14(right_shift_20_out_14), .out_15(right_shift_20_out_15),
    .out_16(right_shift_20_out_16));
  right_shift right_shift_21 (
    .in_1(right_shift_22_out_9), .in_2(right_shift_22_out_10), .in_3(right_shift_22_out_11),
    .in_4(right_shift_22_out_12), .in_5(right_shift_22_out_13), .in_6(right_shift_22_out_14),
    .in_7(right_shift_22_out_15), .in_8(right_shift_22_out_16), .out_9(right_shift_21_out_9),
    .out_10(right_shift_21_out_10), .out_11(right_shift_21_out_11), .out_12(right_shift_21_out_12),
    .out_13(right_shift_21_out_13), .out_14(right_shift_21_out_14), .out_15(right_shift_21_out_15),
    .out_16(right_shift_21_out_16));
  right_shift right_shift_22 (
    .in_1(right_shift_14_out_9), .in_2(right_shift_14_out_10), .in_3(right_shift_14_out_11),
    .in_4(right_shift_14_out_12), .in_5(right_shift_14_out_13), .in_6(right_shift_14_out_14),
    .in_7(right_shift_14_out_15), .in_8(right_shift_14_out_16), .out_9(right_shift_22_out_9),
    .out_10(right_shift_22_out_10), .out_11(right_shift_22_out_11), .out_12(right_shift_22_out_12),
    .out_13(right_shift_22_out_13), .out_14(right_shift_22_out_14), .out_15(right_shift_22_out_15),
    .out_16(right_shift_22_out_16));
  right_shift right_shift_23 (
    .in_1(right_shift_18_out_9), .in_2(right_shift_18_out_10), .in_3(right_shift_18_out_11),
    .in_4(right_shift_18_out_12), .in_5(right_shift_18_out_13), .in_6(right_shift_18_out_14),
    .in_7(right_shift_18_out_15), .in_8(right_shift_18_out_16), .out_9(right_shift_23_out_9),
    .out_10(right_shift_23_out_10), .out_11(right_shift_23_out_11), .out_12(right_shift_23_out_12),
    .out_13(right_shift_23_out_13), .out_14(right_shift_23_out_14), .out_15(right_shift_23_out_15),
    .out_16(right_shift_23_out_16));
  right_shift right_shift_24 (
    .in_1(right_shift_23_out_9), .in_2(right_shift_23_out_10), .in_3(right_shift_23_out_11),
    .in_4(right_shift_23_out_12), .in_5(right_shift_23_out_13), .in_6(right_shift_23_out_14),
    .in_7(right_shift_23_out_15), .in_8(right_shift_23_out_16), .out_9(right_shift_24_out_9),
    .out_10(right_shift_24_out_10), .out_11(right_shift_24_out_11), .out_12(right_shift_24_out_12),
    .out_13(right_shift_24_out_13), .out_14(right_shift_24_out_14), .out_15(right_shift_24_out_15),
    .out_16(right_shift_24_out_16));
  right_shift right_shift_25 (
    .in_1(right_shift_20_out_9), .in_2(right_shift_20_out_10), .in_3(right_shift_20_out_11),
    .in_4(right_shift_20_out_12), .in_5(right_shift_20_out_13), .in_6(right_shift_20_out_14),
    .in_7(right_shift_20_out_15), .in_8(right_shift_20_out_16), .out_9(right_shift_25_out_9[0]),
    .out_10(right_shift_25_out_9[1]), .out_11(right_shift_25_out_9[2]), .out_12(right_shift_25_out_9[3]),
    .out_13(right_shift_25_out_9[4]), .out_14(right_shift_25_out_9[5]), .out_15(right_shift_25_out_9[6]),
    .out_16(right_shift_25_out_9[7]));
  Adder_usado_na_multiplicacao adder_usado_na_multiplicacao_6 (
    .in_1(right_shift_25_out_9), .in_2(adder_usado_na_multiplicacao_5_out_4),
    .overflow(adder_usado_na_multiplicacao_6_overflow), .out_4(adder_usado_na_multiplicacao_6_out_4));
  right_shift right_shift_26 (
    .in_1(right_shift_24_out_9), .in_2(right_shift_24_out_10), .in_3(right_shift_24_out_11),
    .in_4(right_shift_24_out_12), .in_5(right_shift_24_out_13), .in_6(right_shift_24_out_14),
    .in_7(right_shift_24_out_15), .in_8(right_shift_24_out_16), .out_9(right_shift_26_out_9),
    .out_10(right_shift_26_out_10), .out_11(right_shift_26_out_11), .out_12(right_shift_26_out_12),
    .out_13(right_shift_26_out_13), .out_14(right_shift_26_out_14), .out_15(right_shift_26_out_15),
    .out_16(right_shift_26_out_16));
  right_shift right_shift_27 (
    .in_1(right_shift_28_out_9), .in_2(right_shift_28_out_10), .in_3(right_shift_28_out_11),
    .in_4(right_shift_28_out_12), .in_5(right_shift_28_out_13), .in_6(right_shift_28_out_14),
    .in_7(right_shift_28_out_15), .in_8(right_shift_28_out_16), .out_9(right_shift_27_out_9[0]),
    .out_10(right_shift_27_out_9[1]), .out_11(right_shift_27_out_9[2]), .out_12(right_shift_27_out_9[3]),
    .out_13(right_shift_27_out_9[4]), .out_14(right_shift_27_out_9[5]), .out_15(right_shift_27_out_9[6]),
    .out_16(right_shift_27_out_9[7]));
  right_shift right_shift_28 (
    .in_1(right_shift_26_out_9), .in_2(right_shift_26_out_10), .in_3(right_shift_26_out_11),
    .in_4(right_shift_26_out_12), .in_5(right_shift_26_out_13), .in_6(right_shift_26_out_14),
    .in_7(right_shift_26_out_15), .in_8(right_shift_26_out_16), .out_9(right_shift_28_out_9),
    .out_10(right_shift_28_out_10), .out_11(right_shift_28_out_11), .out_12(right_shift_28_out_12),
    .out_13(right_shift_28_out_13), .out_14(right_shift_28_out_14), .out_15(right_shift_28_out_15),
    .out_16(right_shift_28_out_16));
  Adder_usado_na_multiplicacao adder_usado_na_multiplicacao_7 (
    .in_1(right_shift_27_out_9), .in_2(adder_usado_na_multiplicacao_6_out_4),
    .overflow(adder_usado_na_multiplicacao_7_overflow), .out_4(out_11));
  or or_1 (in_10, adder_usado_na_multiplicacao_7_overflow, adder_usado_na_multiplicacao_6_overflow, adder_usado_na_multiplicacao_5_overflow, adder_usado_na_multiplicacao_4_overflow, adder_usado_na_multiplicacao_3_overflow, adder_usado_na_multiplicacao_2_overflow, adder_usado_na_multiplicacao_1_overflow);
endmodule

module ALU (
  input  [7:0] in_1,
  input  [7:0] in_2,
  input  [2:0] in_3,
  output [7:0] out_4,
  output out_5
);

  wire [7:0] demultiplexer_1_out0, demultiplexer_1_out1, demultiplexer_2_out0, demultiplexer_2_out1,
       demultiplexer_3_out0, demultiplexer_3_out1, demultiplexer_4_out0, demultiplexer_4_out1,
       demultiplexer_5_out0, demultiplexer_5_out1, demultiplexer_6_out0, multi_1_out_11,
       n8_bit_riple_carry_adder_1_out_6;

  Demultiplexer #(.width(8)) demultiplexer_1 (
    .out0(demultiplexer_1_out0), .out1(demultiplexer_1_out1), .in(in_1), .sel(in_3[2]));  // open: en
  Demultiplexer #(.width(8)) demultiplexer_2 (
    .out0(demultiplexer_2_out0), .out1(demultiplexer_2_out1), .in(in_2), .sel(in_3[2]));  // open: en
  Demultiplexer #(.width(8)) demultiplexer_3 (
    .out0(demultiplexer_3_out0), .out1(demultiplexer_3_out1), .in(demultiplexer_1_out0), .sel(in_3[1]));  // open: en
  Demultiplexer #(.width(8)) demultiplexer_4 (
    .out0(demultiplexer_4_out0), .out1(demultiplexer_4_out1), .in(demultiplexer_3_out1), .sel(in_3[0]));  // open: en
  Demultiplexer #(.width(8)) demultiplexer_5 (
    .out0(demultiplexer_5_out0), .out1(demultiplexer_5_out1), .in(demultiplexer_2_out0), .sel(in_3[1]));  // open: en
  Demultiplexer #(.width(8)) demultiplexer_6 (
    .out0(demultiplexer_6_out0), .in(demultiplexer_5_out1), .sel(in_3[0]));  // open: out1, en
  _8_bit_Riple_Carry_Adder u_8_bit_riple_carry_adder_1 (
    .OP_Code(in_3[0]), .Carry_Inicial(1'b0), .overflow(out_5), .in_2(demultiplexer_3_out0),
    .in_1(demultiplexer_5_out0), .out_6(n8_bit_riple_carry_adder_1_out_6));
  multi multi_1 (
    .B7(demultiplexer_4_out0[7]), .B6(demultiplexer_4_out0[6]), .B5(demultiplexer_4_out0[5]),
    .B4(demultiplexer_4_out0[4]), .in_5(demultiplexer_6_out0), .B3(demultiplexer_4_out0[3]),
    .B2(demultiplexer_4_out0[2]), .B1(demultiplexer_4_out0[1]), .B0(demultiplexer_4_out0[0]),
    .out_11(multi_1_out_11), .in_10(out_5));
  Multiplexer #(.width(8)) multiplexer_1 (
    .in0(n8_bit_riple_carry_adder_1_out_6), .in1(multi_1_out_11), .out(out_4), .sel(in_3[1]));  // open: en

  // Notes on the sheet:
  //   div resto
  //   div resto
  //   soma/subtra
  //   mult
  //   soma/subtra
  //   soma
  //   div
endmodule

module right_shift (
  input  in_1,
  input  in_2,
  input  in_3,
  input  in_4,
  input  in_5,
  input  in_6,
  input  in_7,
  input  in_8,
  output out_9,
  output out_10,
  output out_11,
  output out_12,
  output out_13,
  output out_14,
  output out_15,
  output out_16
);


  assign out_9 = 1'b0;
  assign out_10 = in_1;
  assign out_11 = in_2;
  assign out_12 = in_3;
  assign out_13 = in_4;
  assign out_14 = in_5;
  assign out_15 = in_6;
  assign out_16 = in_7;
  // also tied to GND on the sheet: in_8
endmodule

module And (
  input  in_1,
  input  in_2,
  input  in_3,
  input  in_4,
  input  in_5,
  input  in_6,
  input  in_7,
  input  in_8,
  input  in_9,
  output out_10,
  output out_11,
  output out_12,
  output out_13,
  output out_14,
  output out_15,
  output out_16,
  output out_17
);

  and and_1 (out_17, in_8, in_9);
  and and_2 (out_16, in_7, in_9);
  and and_3 (out_15, in_6, in_9);
  and and_4 (out_14, in_5, in_9);
  and and_5 (out_13, in_4, in_9);
  and and_6 (out_12, in_3, in_9);
  and and_7 (out_11, in_2, in_9);
  and and_8 (out_10, in_1, in_9);
endmodule

module Adder_usado_na_multiplicacao (
  input  [7:0] in_1,
  input  [7:0] in_2,
  output overflow,
  output [7:0] out_4
);

  wire full_adder_2_carry_bit, full_adder_3_carry_bit, full_adder_4_carry_bit, full_adder_5_carry_bit,
       full_adder_6_carry_bit, full_adder_7_carry_bit, full_adder_8_carry_bit;

  Full_Adder full_adder_1 (
    .a(in_2[7]), .b(in_1[7]), .c__carry(full_adder_2_carry_bit), .Carry_Bit(overflow), .Answer_Bit(out_4[7]));
  Full_Adder full_adder_2 (
    .a(in_2[6]), .b(in_1[6]), .c__carry(full_adder_3_carry_bit), .Carry_Bit(full_adder_2_carry_bit),
    .Answer_Bit(out_4[6]));
  Full_Adder full_adder_3 (
    .a(in_2[5]), .b(in_1[5]), .c__carry(full_adder_4_carry_bit), .Carry_Bit(full_adder_3_carry_bit),
    .Answer_Bit(out_4[5]));
  Full_Adder full_adder_4 (
    .a(in_2[4]), .b(in_1[4]), .c__carry(full_adder_5_carry_bit), .Carry_Bit(full_adder_4_carry_bit),
    .Answer_Bit(out_4[4]));
  Full_Adder full_adder_5 (
    .a(in_2[3]), .b(in_1[3]), .c__carry(full_adder_6_carry_bit), .Carry_Bit(full_adder_5_carry_bit),
    .Answer_Bit(out_4[3]));
  Full_Adder full_adder_6 (
    .a(in_2[2]), .b(in_1[2]), .c__carry(full_adder_7_carry_bit), .Carry_Bit(full_adder_6_carry_bit),
    .Answer_Bit(out_4[2]));
  Full_Adder full_adder_7 (
    .a(in_2[1]), .b(in_1[1]), .c__carry(full_adder_8_carry_bit), .Carry_Bit(full_adder_7_carry_bit),
    .Answer_Bit(out_4[1]));
  Full_Adder full_adder_8 (
    .a(in_2[0]), .b(in_1[0]), .c__carry(1'b0), .Carry_Bit(full_adder_8_carry_bit), .Answer_Bit(out_4[0]));
endmodule

module contador (
  input  Enable,
  input  Reset_Assincrono,
  input  Clock,
  output [7:0] Valor
);

  wire [7:0] n8_bit_riple_carry_adder_1_out_6;

  _8_bit_Riple_Carry_Adder u_8_bit_riple_carry_adder_1 (
    .OP_Code(1'b0), .Carry_Inicial(1'b0), .in_2(8'h1), .in_1(Valor), .out_6(n8_bit_riple_carry_adder_1_out_6));  // open: overflow
  Register register_1 (
    .D(n8_bit_riple_carry_adder_1_out_6), .en(Enable), .Q(Valor), .clk(Clock), .clr(Reset_Assincrono));
endmodule

module clock2 (
  output [7:0] out_1
);

  wire clock_1_out, clock_2_out;

  Clock clock_1 (.out(clock_1_out));
  Clock clock_2 (.out(clock_2_out));
  contador contador_1 (.Enable(clock_1_out), .Reset_Assincrono(clock_2_out), .Valor(out_1));  // open: Clock
endmodule

module Divisor (
  input  [7:0] a___Dividendo,
  input  [7:0] b___Divisor,
  output [7:0] out_3,
  output [7:0] out_4
);

  wire clock_1_out, clock_2_out, Clock_geral_da_divisao_out, not_1_out, x_0_1_out_2, x_0_2_out_2;
  wire [7:0] multiplexer_1_out, register_1_q;

  contador contador_1 (
    .Enable(not_1_out), .Clock(Clock_geral_da_divisao_out), .Reset_Assincrono(clock_1_out), .Valor(out_3));
  Clock clock_1 (.out(clock_1_out));
  x_0 x_0_1 (.in_1(out_3), .out_2(x_0_1_out_2));
  x___0 x_0_2 (.in_1(multiplexer_1_out), .out_2(x_0_2_out_2));
  not not_1 (not_1_out, x_0_2_out_2);
  Multiplexer #(.width(8)) multiplexer_1 (
    .in0(out_4), .in1(a___Dividendo), .out(multiplexer_1_out), .sel(x_0_1_out_2));  // open: en
  Register register_1 (
    .D(multiplexer_1_out), .en(not_1_out), .Q(register_1_q), .clk(Clock_geral_da_divisao_out),
    .clr(clock_2_out));
  Clock clock_2 (.out(clock_2_out));
  Clock Clock_geral_da_divisao (.out(Clock_geral_da_divisao_out));
  _8_bit_Riple_Carry_Adder u_8_bit_riple_carry_adder_1 (
    .OP_Code(1'b1), .Carry_Inicial(1'b0), .in_2(register_1_q), .in_1(b___Divisor), .out_6(out_4));  // open: overflow
endmodule

module x_0 (
  input  [7:0] in_1,
  output out_2
);

  nor nor_1 (out_2, in_1[0], in_1[1], in_1[2], in_1[3], in_1[4], in_1[5], in_1[6], in_1[7]);
endmodule

module x___0 (
  input  [7:0] in_1,
  output out_2
);


  assign out_2 = in_1[7];
  // also tied to GND on the sheet: {in_1[0], in_1[1], in_1[2], in_1[3], in_1[4], in_1[5], in_1[6]}
endmodule
