// Logisim project ep4.1.6.circ as structural Verilog: 19 circuits, main circuit CPU
module CPU (
  input  Reset_Manual,
  input  Reset_RAM,
  input  Clock_Manual_RAM,
  input  Manual_Write_Read_Option,
  input  [7:0] Manual_Write_Address,
  input  ON_OFF,
  input  [15:0] Data_In_Manual,
  output Estatus_do_Circuito,
  output \Divisão_por_Zero ,
  output Overflow
);

  wire Clock_Master, Clock_Master_out, Conditional_Jump, Disable_Circuit, Overflow_t, Zero_Division;
  wire [1:0] ACC_Binary_Command, IR_command, RAM_Binary_Command;
  wire [3:0] PC_Binary_Command;
  wire [7:0] Address_IR____PC, Instruction, RAM_Reading_Address;
  wire [8:0] ULA_Binary_Command;
  wire [15:0] ACC____ULA, Data_In, Data_Out, Data_RAM____IR, RAM____ULA, ULA____ACC_Out;

  IR ir_1 (
    .Clear_IR(Reset_Manual), .IR_Binary_Code_In(IR_command), .Address_IR____PC_Out(Address_IR____PC),
    .Data_RAM____IR_In(Data_RAM____IR), .Command_Out(Instruction));
  Clock u_Clock_Master (.out(Clock_Master_out));
  Memory_Ram memory_ram_1 (
    .PC_Reading_Address(RAM_Reading_Address), .Manual_Option(Manual_Write_Read_Option),
    .Clock_Manual(Clock_Manual_RAM), .Reset_RAM(Reset_RAM), .Data_Manual_In(Data_In_Manual),
    .RAM_binary_Command(RAM_Binary_Command), .Data_ACC____RAM(Data_Out), .Data_RAM____ACC(Data_In),
    .Data_RAM____IR_Out(Data_RAM____IR), .Manual_Write_Address(Manual_Write_Address));
  Power_Circuit power_circuit_1 (
    .Clock_Principal(Clock_Master_out), .Disable_Option(Disable_Circuit), .Power_On(ON_OFF),
    .Clock_Principal_2(Clock_Master), .Estado_do_Circuito(Estatus_do_Circuito), .Overflow_In(Overflow_t),
    .Zero_division_In(Zero_Division), .Zero_division_Out(\Divisão_por_Zero ), .Overflow_Out(Overflow),
    .Forced_Reset(Reset_Manual));
  CTRL ctrl_1 (
    .PC_Binary_Code_Out(PC_Binary_Command), .IR_Binary_Code_Out(IR_command),
    .RAM_Binary_Code_Out(RAM_Binary_Command), .Disable_Circuit(Disable_Circuit), .Clock_Master(Clock_Master),
    .Instruction(Instruction), .Clear_FDX_Manual(Reset_Manual), .ACC_Binary_Code_Out(ACC_Binary_Command),
    .ULA_Binary_Code_Out(ULA_Binary_Command), .Conditional_Jump(Conditional_Jump));
  ACC acc_1 (
    .clear(Reset_Manual), .ACC_binary_Command(ACC_Binary_Command), .RAM_Data_In(Data_In),
    .Data_Out(Data_Out), .ULA_Data_In(ULA____ACC_Out));
  PC pc_1 (
    .Address_IR____PC(Address_IR____PC), .RAM_Reading_Address(RAM_Reading_Address),
    .PC_Binary_Code_In(PC_Binary_Command), .Clear_Manual(Reset_Manual));
  ULA ula_1 (
    .ULA_Binary_Code_IN(ULA_Binary_Command), .RAM____ULA(RAM____ULA), .ACC____ULA(ACC____ULA),
    .Clock_Geral(Clock_Master), .ULA____ACC(ULA____ACC_Out), .Conditional_Jump(Conditional_Jump),
    .clear(Reset_Manual), .overflow(Overflow_t), .div_0(Zero_Division));

  // Other names for the same wires on the sheet: Clear_RAM = Reset_RAM; Clock_RAM = Clock_Manual_RAM;
  //   Data_Manual_In[15:0] = Data_In_Manual; Manual_Option = Manual_Write_Read_Option; Clear_ACC = Reset_Manual;
  //   Clear_FDX_Manual = Reset_Manual; Clear_IR = Reset_Manual; Clear_Pc = Reset_Manual; Clear_ULA = Reset_Manual;
  //   Power_Reset = Reset_Manual; Reset_Geral = Reset_Manual

  // Notes on the sheet:
  //   Adicionar as seguintes coisas:
  //   ULA, sequenciador de jumps condicionais e uma input mais amigável
  //   Resete os circuitos com o "Reset Manual"
  //   Para executar insira manualmente dados na RAM
  //   De um Push no botão ON/OFF e ligue o clock do sistema
  //   Quando o programa chegar ao fim o LED "Estatus do Circuito" estará apagado e as manipulações de dados terão terminado.
  //   PS: Ao terminar de inserir/resetar dados deixe as entradas zeradas.
  //   Escrita/Leitura na RAM:
  //   Escrita  - 1
  //   Leitura - 0
endmodule

// RAM
module Memory_Ram (
  input  [15:0] Data_ACC____RAM,
  input  [15:0] Data_Manual_In,
  input  [7:0] PC_Reading_Address,
  input  [7:0] Manual_Write_Address,
  input  Reset_RAM,
  input  Clock_Manual,
  input  Manual_Option,
  input  [1:0] RAM_binary_Command,
  output [15:0] Data_RAM____ACC,
  output [15:0] Data_RAM____IR_Out
);

  wire Clock_Flag, not_1_out, not_2_out, Read_Write_Flag, temp_flag;
  wire [7:0] multiplexer_3_out;
  wire [15:0] multiplexer_2_out;

  Multiplexer #(.enable("false")) multiplexer_1 (
    .in0(RAM_binary_Command[1]), .in1(Clock_Manual), .out(Clock_Flag), .sel(Manual_Option));
  Multiplexer #(.width(16), .enable("false")) multiplexer_2 (
    .in0(Data_ACC____RAM), .in1(Data_Manual_In), .out(multiplexer_2_out), .sel(not_1_out));
  not not_1 (not_1_out, temp_flag);
  assign Data_RAM____ACC = Read_Write_Flag ? multiplexer_2_out : 16'bz;  // Controlled_Buffer controlled_buffer_1
  Multiplexer #(.width(8), .enable("false")) multiplexer_3 (
    .in0(PC_Reading_Address), .in1(Manual_Write_Address), .out(multiplexer_3_out), .sel(Manual_Option));
  not not_2 (not_2_out, Read_Write_Flag);
  RAM #(.dataWidth(16)) ram_1 (
    .addr(multiplexer_3_out), .data(Data_RAM____ACC), .sel(1'b1), .clk(Clock_Flag), .ld(not_2_out),
    .clr(Reset_RAM));
  or or_1 (Read_Write_Flag, Manual_Option, temp_flag);
  J_K_Flip_Flop j_k_ff_1 (
    .J(1'b1), .clk(RAM_binary_Command[0]), .K(1'b1), .Q(temp_flag), .reset(Clock_Flag));  // open: Qn, preset, en

  assign Data_RAM____IR_Out = Data_RAM____ACC;

  // Other names for the same wires on the sheet: Manual_Frag = Manual_Option; Write_OPT_RAM = RAM_binary_Command[0];
  //   Clock_Write_ACC_____RAM = RAM_binary_Command[1]
endmodule

module PC (
  input  Clear_Manual,
  input  [7:0] Address_IR____PC,
  input  [3:0] PC_Binary_Code_In,
  output [7:0] RAM_Reading_Address
);

  wire multiplexer_1_out;
  wire [7:0] multiplexer_2_out, PC_Buffer_Out;

  Multiplexer #(.enable("false")) multiplexer_1 (
    .in0(PC_Binary_Code_In[2]), .in1(Clear_Manual), .out(multiplexer_1_out), .sel(Clear_Manual));
  Multiplexer #(.width(8), .enable("false")) multiplexer_2 (
    .in0(Address_IR____PC), .in1(PC_Buffer_Out), .out(multiplexer_2_out), .sel(PC_Binary_Code_In[3]));
  Bloco_Flip_Fliop bloco_flip_fliop_1 (
    .Clear(multiplexer_1_out), ._8_bits_Input(multiplexer_2_out), ._8_bits_Output(RAM_Reading_Address),
    .Clock(PC_Binary_Code_In[0]));  // open: Overflow
  Register Register (
    .D(RAM_Reading_Address), .en(1'b1), .Q(PC_Buffer_Out), .clk(PC_Binary_Code_In[1]), .clr(Clear_Manual));

  // Other names for the same wires on the sheet: Clock_PC = PC_Binary_Code_In[0];
  //   Clock_Buffer_PC = PC_Binary_Code_In[1]; Clear_PC = PC_Binary_Code_In[2];
  //   Restaura_Buffer_PC = PC_Binary_Code_In[3]; PC_Buffer_In[7:0] = RAM_Reading_Address
endmodule

module Bloco_Flip_Fliop (
  input  Clear,
  input  Clock,
  input  [7:0] _8_bits_Input,
  output Overflow,
  output [7:0] _8_bits_Output
);

  wire and_1_out, and_2_out, and_3_out, and_4_out, and_5_out, and_6_out;

  J_K_Flip_Flop j_k_ff_1 (
    .J(1'b1), .clk(Clock), .K(1'b1), .Q(_8_bits_Output[0]), .preset(_8_bits_Input[0]), .reset(Clear));  // open: Qn, en
  J_K_Flip_Flop j_k_ff_2 (
    .J(_8_bits_Output[0]), .clk(Clock), .K(_8_bits_Output[0]), .Q(_8_bits_Output[1]),
    .preset(_8_bits_Input[1]), .reset(Clear));  // open: Qn, en
  and and_1 (and_1_out, _8_bits_Output[0], _8_bits_Output[1]);
  and and_2 (and_2_out, and_1_out, _8_bits_Output[2]);
  J_K_Flip_Flop j_k_ff_3 (
    .J(and_1_out), .clk(Clock), .K(and_1_out), .Q(_8_bits_Output[2]), .preset(_8_bits_Input[2]), .reset(Clear));  // open: Qn, en
  J_K_Flip_Flop j_k_ff_4 (
    .J(and_2_out), .clk(Clock), .K(and_2_out), .Q(_8_bits_Output[3]), .preset(_8_bits_Input[3]), .reset(Clear));  // open: Qn, en
  and and_3 (and_3_out, and_2_out, _8_bits_Output[3]);
  J_K_Flip_Flop j_k_ff_5 (
    .J(and_3_out), .clk(Clock), .K(and_3_out), .Q(_8_bits_Output[4]), .preset(_8_bits_Input[4]), .reset(Clear));  // open: Qn, en
  and and_4 (and_4_out, and_3_out, _8_bits_Output[4]);
  J_K_Flip_Flop j_k_ff_6 (
    .J(and_4_out), .clk(Clock), .K(and_4_out), .Q(_8_bits_Output[5]), .preset(_8_bits_Input[5]), .reset(Clear));  // open: Qn, en
  and and_5 (and_5_out, and_4_out, _8_bits_Output[5]);
  J_K_Flip_Flop j_k_ff_7 (
    .J(and_5_out), .clk(Clock), .K(and_5_out), .Q(_8_bits_Output[6]), .preset(_8_bits_Input[6]), .reset(Clear));  // open: Qn, en
  and and_6 (and_6_out, and_5_out, _8_bits_Output[6]);
  J_K_Flip_Flop j_k_ff_8 (
    .J(and_6_out), .clk(Clock), .K(and_6_out), .Q(_8_bits_Output[7]), .preset(_8_bits_Input[7]), .reset(Clear));  // open: Qn, en
  and and_7 (Overflow, and_6_out, _8_bits_Output[7]);

  // Other names for the same wires on the sheet: In1 = _8_bits_Input[0]; In2 = _8_bits_Input[1];
  //   In3 = _8_bits_Input[2]; In4 = _8_bits_Input[3]; In5 = _8_bits_Input[4]; In6 = _8_bits_Input[5];
  //   In7 = _8_bits_Input[6]; In8 = _8_bits_Input[7]; Out1 = _8_bits_Output[0]; Out2 = _8_bits_Output[1];
  //   Out3 = _8_bits_Output[2]; Out4 = _8_bits_Output[3]; Out5 = _8_bits_Output[4]; Out6 = _8_bits_Output[5];
  //   Out7 = _8_bits_Output[6]; Out8 = _8_bits_Output[7]; over = Overflow
endmodule

module IR (
  input  [15:0] Data_RAM____IR_In,
  input  Clear_IR,
  input  [1:0] IR_Binary_Code_In,
  output [7:0] Command_Out,
  output [7:0] Address_IR____PC_Out
);

  wire [7:0] Address_IR____PC;

  Multiplexer #(.width(8)) multiplexer_1 (
    .in0({8{1'b0}}), .in1(Address_IR____PC), .out(Address_IR____PC_Out), .sel(IR_Binary_Code_In[1]));  // open: en
  Register #(.width(16)) Register (
    .D(Data_RAM____IR_In), .en(1'b1), .Q({Command_Out, Address_IR____PC}), .clk(IR_Binary_Code_In[0]),
    .clr(Clear_IR));

  // Other names for the same wires on the sheet: Command[7:0] = Command_Out; Clock_IR = IR_Binary_Code_In[0];
  //   Clock_ADD_IR____PC = IR_Binary_Code_In[1]
endmodule

module ACC (
  input  [15:0] RAM_Data_In,
  input  [15:0] ULA_Data_In,
  input  clear,
  input  [1:0] ACC_binary_Command,
  output [15:0] Data_Out
);

  wire temp_flag;
  wire [15:0] multiplexer_1_out;

  Multiplexer #(.width(16), .enable("false")) multiplexer_1 (
    .in0(RAM_Data_In), .in1(ULA_Data_In), .out(multiplexer_1_out), .sel(temp_flag));
  Register #(.width(16)) Acumulador (
    .D(multiplexer_1_out), .en(1'b1), .Q(Data_Out), .clk(ACC_binary_Command[0]), .clr(clear));
  J_K_Flip_Flop j_k_ff_1 (
    .J(1'b1), .clk(ACC_binary_Command[1]), .K(1'b1), .Q(temp_flag), .reset(ACC_binary_Command[0]));  // open: Qn, preset, en

  // Other names for the same wires on the sheet: ACC_Clock = ACC_binary_Command[0];
  //   ACC_Clock_Shift_Option = ACC_binary_Command[1]
endmodule

// Controlador
module CTRL (
  input  Clock_Master,
  input  Clear_FDX_Manual,
  input  [7:0] Instruction,
  input  Conditional_Jump,
  output [3:0] PC_Binary_Code_Out,
  output [1:0] RAM_Binary_Code_Out,
  output [1:0] IR_Binary_Code_Out,
  output [1:0] ACC_Binary_Code_Out,
  output Disable_Circuit,
  output [8:0] ULA_Binary_Code_Out
);

  wire Clear_FDX, Clear_PC, Clear_PC2, Clear_PC2_Flag, Clear_PC2_ULA_Flag, Clock_FDX, Clock_Geral,
       Clock_Instruction, Command_Enable, controlled_buffer_9_out, controlled_buffer_13_out,
       controlled_buffer_17_out, controlled_buffer_22_out, controlled_buffer_23_out,
       controlled_buffer_34_out, Feedback_JMP, Feedback_LDA, Feedback_NOP, Feedback_STA, Feedback_STP,
       Feedback_ULA_cmd, INN, JDZ, JEQ, JGE, JGT, JLE, JLT, JMP, jmp_1_clear_pc, jmp_1_clock_add_ir_____pc,
       jmp_1_feedback_jmp, jmp_1_restaura_buffer_pc, LDA, lda_1_clear_pc, lda_1_clear_pc_2,
       lda_1_clock_add_ir____pc, lda_1_clock_buffer_pc, lda_1_clock_read_ram_____acc, lda_1_feedback_lda,
       lda_1_restaura_buffer_pc, NOP, nop_1_feedback_nop, PRN, STA, sta_1_clear_pc, sta_1_clear_pc_2,
       sta_1_clock_add_ir_____pc, sta_1_clock_buffer_pc, sta_1_clock_write_acc_____ram, sta_1_feedback_sta,
       sta_1_restaura_buffer_pc, sta_1_write_opt_ram, STP, stp_1_clear_pc, stp_1_disable_circuit,
       stp_1_feedback_stp, ula_cmd_1_clear_pc, ula_cmd_1_clock_add_ir____pc, ula_cmd_1_clock_buffer_pc,
       ula_cmd_1_clock_read_acc_____ula, ula_cmd_1_clock_read_ram_____ula, ula_cmd_1_clock_ula_operation,
       ula_cmd_1_clock_write_acc, ula_cmd_1_clock_write_ula_____acc, ula_cmd_1_feedback_ula_cmd,
       ula_cmd_1_restaura_buffer_pc, ULA_Instruction;

  LDA lda_1 (
    .Clock_Geral(Clock_Geral), .LDA_Enable(LDA), .Clock_Buffer_PC(lda_1_clock_buffer_pc),
    .Clear_PC(lda_1_clear_pc), .Clock_ADD_IR____PC(lda_1_clock_add_ir____pc),
    .Restaura_Buffer_PC(lda_1_restaura_buffer_pc), .FeedBack_LDA(lda_1_feedback_lda),
    .Clear_PC_2(lda_1_clear_pc_2), .Clock_Read_RAM_____ACC(lda_1_clock_read_ram_____acc),
    .Clear_manual(Clear_FDX_Manual));
  STA sta_1 (
    .Clock_Geral(Clock_Geral), .STA_Enable(STA), .Clock_Buffer_PC(sta_1_clock_buffer_pc),
    .Clear_PC(sta_1_clear_pc), .Clock_ADD_IR_____PC(sta_1_clock_add_ir_____pc),
    .Write_OPT_RAM(sta_1_write_opt_ram), .FeedBack_STA(sta_1_feedback_sta),
    .Clock_Write_ACC_____RAM(sta_1_clock_write_acc_____ram), .Clear_PC_2(sta_1_clear_pc_2),
    .Restaura_Buffer_PC(sta_1_restaura_buffer_pc), .Clear_manual(Clear_FDX_Manual));
  JMP jmp_1 (
    .Clock_Geral(Clock_Geral), .JMP_Enable(JMP), .Clear_PC(jmp_1_clear_pc),
    .Clock_ADD_IR_____PC(jmp_1_clock_add_ir_____pc), .FeedBack_JMP(jmp_1_feedback_jmp),
    .Clear_manual(Clear_FDX_Manual), .Restaura_Buffer_PC(jmp_1_restaura_buffer_pc));
  STP stp_1 (
    .Clock_Geral(Clock_Geral), .STP_Enable(STP), .Clear_PC(stp_1_clear_pc),
    .Disable_Circuit(stp_1_disable_circuit), .FeedBack_STP(stp_1_feedback_stp),
    .Clear_manual(Clear_FDX_Manual));
  assign PC_Binary_Code_Out[1] = LDA ? lda_1_clock_buffer_pc : 1'bz;  // Controlled_Buffer controlled_buffer_1
  assign Clear_PC = LDA ? lda_1_clear_pc : 1'bz;  // Controlled_Buffer controlled_buffer_2
  assign IR_Binary_Code_Out[1] = LDA ? lda_1_clock_add_ir____pc : 1'bz;  // Controlled_Buffer controlled_buffer_3
  ExactlyOne xor_1 (.out(Clear_PC2_Flag), .in0(lda_1_clear_pc_2), .in1(Clear_PC2_ULA_Flag), .in2(sta_1_clear_pc_2));
  assign PC_Binary_Code_Out[1] = STA ? sta_1_clock_buffer_pc : 1'bz;  // Controlled_Buffer controlled_buffer_4
  assign Clear_PC = STA ? sta_1_clear_pc : 1'bz;  // Controlled_Buffer controlled_buffer_5
  assign IR_Binary_Code_Out[1] = STA ? sta_1_clock_add_ir_____pc : 1'bz;  // Controlled_Buffer controlled_buffer_6
  assign Clear_PC = JMP ? jmp_1_clear_pc : 1'bz;  // Controlled_Buffer controlled_buffer_7
  assign IR_Binary_Code_Out[1] = JMP ? jmp_1_clock_add_ir_____pc : 1'bz;  // Controlled_Buffer controlled_buffer_8
  assign controlled_buffer_9_out = JMP ? jmp_1_feedback_jmp : 1'bz;  // Controlled_Buffer controlled_buffer_9
  assign PC_Binary_Code_Out[3] = JMP ? jmp_1_restaura_buffer_pc : 1'bz;  // Controlled_Buffer controlled_buffer_10
  assign Clear_PC = STP ? stp_1_clear_pc : 1'bz;  // Controlled_Buffer controlled_buffer_11
  assign Disable_Circuit = STP ? stp_1_disable_circuit : 1'bz;  // Controlled_Buffer controlled_buffer_12
  assign controlled_buffer_13_out = STP ? stp_1_feedback_stp : 1'bz;  // Controlled_Buffer controlled_buffer_13
  assign ACC_Binary_Code_Out[0] = LDA ? lda_1_clock_read_ram_____acc : 1'bz;  // Controlled_Buffer controlled_buffer_14
  assign Clear_PC2 = LDA ? lda_1_clear_pc_2 : 1'bz;  // Controlled_Buffer controlled_buffer_15
  assign PC_Binary_Code_Out[3] = LDA ? lda_1_restaura_buffer_pc : 1'bz;  // Controlled_Buffer controlled_buffer_16
  assign controlled_buffer_17_out = LDA ? lda_1_feedback_lda : 1'bz;  // Controlled_Buffer controlled_buffer_17
  assign RAM_Binary_Code_Out[0] = STA ? sta_1_write_opt_ram : 1'bz;  // Controlled_Buffer controlled_buffer_18
  assign RAM_Binary_Code_Out[1] = STA ? sta_1_clock_write_acc_____ram : 1'bz;  // Controlled_Buffer controlled_buffer_19
  assign Clear_PC2 = STA ? sta_1_clear_pc_2 : 1'bz;  // Controlled_Buffer controlled_buffer_20
  assign PC_Binary_Code_Out[3] = STA ? sta_1_restaura_buffer_pc : 1'bz;  // Controlled_Buffer controlled_buffer_21
  assign controlled_buffer_22_out = STA ? sta_1_feedback_sta : 1'bz;  // Controlled_Buffer controlled_buffer_22
  and and_1 (Feedback_JMP, controlled_buffer_9_out, jmp_1_feedback_jmp);
  and and_2 (Feedback_STP, controlled_buffer_13_out, stp_1_feedback_stp);
  and and_3 (Feedback_LDA, controlled_buffer_17_out, lda_1_feedback_lda);
  and and_4 (Feedback_STA, controlled_buffer_22_out, sta_1_feedback_sta);
  or or_1 (ULA_Instruction, ULA_Binary_Code_Out[4], ULA_Binary_Code_Out[5], ULA_Binary_Code_Out[6], ULA_Binary_Code_Out[7], ULA_Binary_Code_Out[8]);
  NOP nop_1 (
    .Clock_Geral(Clock_Geral), .NOP_Enable(NOP), .FeedBack_NOP(nop_1_feedback_nop),
    .Clear_manual(Clear_FDX_Manual));
  assign controlled_buffer_23_out = NOP ? nop_1_feedback_nop : 1'bz;  // Controlled_Buffer controlled_buffer_23
  and and_5 (Feedback_NOP, controlled_buffer_23_out, nop_1_feedback_nop);
  ULA_cmd ula_cmd_1 (
    .Clock_Geral(Clock_Geral), .ULA_cmd_Enable(ULA_Instruction), .Clear_manual(Clear_FDX_Manual),
    .Clock_Buffer_PC(ula_cmd_1_clock_buffer_pc), .Clear_PC(ula_cmd_1_clear_pc),
    .Clock_ADD_IR____PC(ula_cmd_1_clock_add_ir____pc),
    .Clock_Read_ACC_____ULA(ula_cmd_1_clock_read_acc_____ula),
    .Clock_Read_RAM_____ULA(ula_cmd_1_clock_read_ram_____ula),
    .Clock_ULA_Operation(ula_cmd_1_clock_ula_operation),
    .Clock_Write_ULA_____ACC(ula_cmd_1_clock_write_ula_____acc), .Clear_PC_2(Clear_PC2_ULA_Flag),
    .Restaura_Buffer_PC(ula_cmd_1_restaura_buffer_pc), .Feedback_ULA_cmd(ula_cmd_1_feedback_ula_cmd),
    .Clock_Write_ACC(ula_cmd_1_clock_write_acc));
  assign PC_Binary_Code_Out[1] = ULA_Instruction ? ula_cmd_1_clock_buffer_pc : 1'bz;  // Controlled_Buffer controlled_buffer_24
  assign Clear_PC = ULA_Instruction ? ula_cmd_1_clear_pc : 1'bz;  // Controlled_Buffer controlled_buffer_25
  assign IR_Binary_Code_Out[1] = ULA_Instruction ? ula_cmd_1_clock_add_ir____pc : 1'bz;  // Controlled_Buffer controlled_buffer_26
  assign ULA_Binary_Code_Out[0] = ULA_Instruction ? ula_cmd_1_clock_read_acc_____ula : 1'bz;  // Controlled_Buffer controlled_buffer_27
  assign ULA_Binary_Code_Out[1] = ULA_Instruction ? ula_cmd_1_clock_read_ram_____ula : 1'bz;  // Controlled_Buffer controlled_buffer_28
  assign ULA_Binary_Code_Out[2] = ULA_Instruction ? ula_cmd_1_clock_ula_operation : 1'bz;  // Controlled_Buffer controlled_buffer_29
  assign ACC_Binary_Code_Out[1] = ULA_Instruction ? ula_cmd_1_clock_write_ula_____acc : 1'bz;  // Controlled_Buffer controlled_buffer_30
  assign ACC_Binary_Code_Out[0] = ULA_Instruction ? ula_cmd_1_clock_write_acc : 1'bz;  // Controlled_Buffer controlled_buffer_31
  assign Clear_PC2 = ULA_Instruction ? Clear_PC2_ULA_Flag : 1'bz;  // Controlled_Buffer controlled_buffer_32
  assign PC_Binary_Code_Out[3] = ULA_Instruction ? ula_cmd_1_restaura_buffer_pc : 1'bz;  // Controlled_Buffer controlled_buffer_33
  assign controlled_buffer_34_out = ULA_Instruction ? ula_cmd_1_feedback_ula_cmd : 1'bz;  // Controlled_Buffer controlled_buffer_34
  and and_6 (Feedback_ULA_cmd, controlled_buffer_34_out, ula_cmd_1_feedback_ula_cmd);
  or or_2 (Command_Enable, LDA, STA, NOP, JMP, STP);
  Demultiplexer #(.enable("false")) demultiplexer_1 (
    .out0(Clock_FDX), .out1(Clock_Geral), .in(Clock_Master), .sel(Command_Enable));
  Multiplexer #(.enable("false")) multiplexer_1 (
    .in0(Clear_PC), .in1(Clear_PC2), .out(PC_Binary_Code_Out[2]), .sel(Clear_PC2_Flag));
  or or_3 (Clear_FDX, Feedback_ULA_cmd, Feedback_LDA, Feedback_STA, Feedback_JMP, Feedback_NOP, Feedback_STP, Clear_FDX_Manual);
  Command command_1 (
    .Instruction(Instruction), .Clock_Instruction(Clock_Instruction), .LDA(LDA),
    .ADD(ULA_Binary_Code_Out[4]), .JLE(JLE), .IN(INN), .STA(STA), .SUB(ULA_Binary_Code_Out[5]), .JDZ(JDZ),
    .PRN(PRN), .NOP(NOP), .MUL(ULA_Binary_Code_Out[6]), .JGT(JGT), .JMP(JMP), .DIV(ULA_Binary_Code_Out[7]),
    .JEQ(JEQ), .STP(STP), .REM(ULA_Binary_Code_Out[8]), .JLT(JLT), .JGE(JGE));
  FDX_Init fdx_init_1 (
    .Clock_Geral(Clock_FDX), .Clock_IR(IR_Binary_Code_Out[0]), .Clock_PC(PC_Binary_Code_Out[0]),
    .Clock_Command(Clock_Instruction), .Clear_FDX(Clear_FDX));

  // Other names for the same wires on the sheet: Clock_Read_RAM_____ACC = ACC_Binary_Code_Out[0];
  //   Clock_Write_ULA____ACC = ACC_Binary_Code_Out[1]; C_Jump = Conditional_Jump; Clear_CMD = Clear_FDX_Manual;
  //   Clock_IR = IR_Binary_Code_Out[0]; Clock_ADD_IR____PC = IR_Binary_Code_Out[1]; Clock_PC = PC_Binary_Code_Out[0];
  //   Clock_Buffer_PC = PC_Binary_Code_Out[1]; Clear_PC_Mestre = PC_Binary_Code_Out[2];
  //   Restaura_Buffer_PC = PC_Binary_Code_Out[3]; Write_OPT_RAM = RAM_Binary_Code_Out[0];
  //   Clock_Write_ACC_____RAM = RAM_Binary_Code_Out[1]; Clock_Read_ACC_____ULA = ULA_Binary_Code_Out[0];
  //   Clock_Read_RAM____ULA = ULA_Binary_Code_Out[1]; Clock_ULA_Operation = ULA_Binary_Code_Out[2];
  //   NULL_Operation = ULA_Binary_Code_Out[3]; ADD = ULA_Binary_Code_Out[4]; SUB = ULA_Binary_Code_Out[5];
  //   MUL = ULA_Binary_Code_Out[6]; DIV = ULA_Binary_Code_Out[7]; REM = ULA_Binary_Code_Out[8]

  // Notes on the sheet:
  //   Como saber qual a instrução a ser executada?!
endmodule

module LDA (
  input  Clock_Geral,
  input  LDA_Enable,
  input  Clear_manual,
  output Clock_Buffer_PC,
  output Clear_PC,
  output Clock_ADD_IR____PC,
  output Clock_Read_RAM_____ACC,
  output Clear_PC_2,
  output Restaura_Buffer_PC,
  output FeedBack_LDA
);

  wire and_2_out, Clear, Clock, decoder_1_out1, decoder_1_out2, decoder_1_out3, decoder_1_out4,
       decoder_1_out5, decoder_1_out6, decoder_1_out7, Out1, Out2, Out3;

  J_K_Flip_Flop j_k_ff_1 (.J(1'b1), .clk(Clock), .K(1'b1), .Q(Out1), .reset(Clear));  // open: Qn, preset, en
  and and_1 (Clock, Clock_Geral, LDA_Enable);
  Decoder #(.select(3), .enable("false")) decoder_1 (
    .out1(decoder_1_out1), .out2(decoder_1_out2), .out3(decoder_1_out3), .out4(decoder_1_out4),
    .out5(decoder_1_out5), .out6(decoder_1_out6), .out7(decoder_1_out7), .sel({Out3, Out2, Out1}));  // open: out0
  J_K_Flip_Flop j_k_ff_2 (.J(Out1), .clk(Clock), .K(Out1), .Q(Out2), .reset(Clear));  // open: Qn, preset, en
  and and_2 (and_2_out, Out1, Out2);
  J_K_Flip_Flop j_k_ff_3 (.J(and_2_out), .clk(Clock), .K(and_2_out), .Q(Out3), .reset(Clear));  // open: Qn, preset, en
  and and_3 (Clock_Buffer_PC, decoder_1_out1, LDA_Enable);
  and and_4 (Clear_PC, decoder_1_out2, LDA_Enable);
  and and_5 (Clock_ADD_IR____PC, decoder_1_out3, LDA_Enable);
  and and_6 (Clock_Read_RAM_____ACC, decoder_1_out4, LDA_Enable);
  and and_7 (Clear_PC_2, decoder_1_out5, LDA_Enable);
  and and_8 (Restaura_Buffer_PC, decoder_1_out6, LDA_Enable);
  and and_9 (FeedBack_LDA, decoder_1_out7, LDA_Enable);
  Multiplexer #(.enable("false")) multiplexer_1 (
    .in0(FeedBack_LDA), .in1(Clear_manual), .out(Clear), .sel(Clear_manual));

  // Other names for the same wires on the sheet: Clear_Automático = FeedBack_LDA
endmodule

module STA (
  input  Clock_Geral,
  input  STA_Enable,
  input  Clear_manual,
  output Clock_Buffer_PC,
  output Clear_PC,
  output Clock_ADD_IR_____PC,
  output Write_OPT_RAM,
  output Clock_Write_ACC_____RAM,
  output Clear_PC_2,
  output Restaura_Buffer_PC,
  output FeedBack_STA
);

  wire and_2_out, and_11_out, Clear, Clock, decoder_1_out1, decoder_1_out2, decoder_1_out3, decoder_1_out4,
       decoder_1_out5, decoder_1_out6, decoder_1_out7, decoder_1_out8, Out1, Out2, Out3, Out4;

  J_K_Flip_Flop j_k_ff_1 (.J(1'b1), .clk(Clock), .K(1'b1), .Q(Out1), .reset(Clear));  // open: Qn, preset, en
  Decoder #(.select(4), .enable("false")) decoder_1 (
    .out1(decoder_1_out1), .out2(decoder_1_out2), .out3(decoder_1_out3), .out4(decoder_1_out4),
    .out5(decoder_1_out5), .out6(decoder_1_out6), .out7(decoder_1_out7), .out8(decoder_1_out8),
    .sel({Out4, Out3, Out2, Out1}));  // open: out0, out9, out10, out11, out12, out13, out14, out15
  and and_1 (Clock, Clock_Geral, STA_Enable);
  and and_2 (and_2_out, Out1, Out2);
  J_K_Flip_Flop j_k_ff_2 (.J(Out1), .clk(Clock), .K(Out1), .Q(Out2), .reset(Clear));  // open: Qn, preset, en
  and and_3 (Clock_Buffer_PC, decoder_1_out1, STA_Enable);
  and and_4 (Clear_PC, decoder_1_out2, STA_Enable);
  and and_5 (Clock_ADD_IR_____PC, decoder_1_out3, STA_Enable);
  and and_6 (Write_OPT_RAM, decoder_1_out4, STA_Enable);
  and and_7 (Clock_Write_ACC_____RAM, decoder_1_out5, STA_Enable);
  and and_8 (Clear_PC_2, decoder_1_out6, STA_Enable);
  and and_9 (Restaura_Buffer_PC, decoder_1_out7, STA_Enable);
  and and_10 (FeedBack_STA, decoder_1_out8, STA_Enable);
  J_K_Flip_Flop j_k_ff_3 (.J(and_2_out), .clk(Clock), .K(and_2_out), .Q(Out3), .reset(Clear));  // open: Qn, preset, en
  and and_11 (and_11_out, and_2_out, Out3);
  J_K_Flip_Flop j_k_ff_4 (
    .J(and_11_out), .clk(Clock), .K(and_11_out), .Q(Out4), .reset(Clear));  // open: Qn, preset, en
  Multiplexer #(.enable("false")) multiplexer_1 (
    .in0(FeedBack_STA), .in1(Clear_manual), .out(Clear), .sel(Clear_manual));

  // Other names for the same wires on the sheet: Clear_Automático = FeedBack_STA
endmodule

module JMP (
  input  Clock_Geral,
  input  JMP_Enable,
  input  Clear_manual,
  output Clear_PC,
  output Clock_ADD_IR_____PC,
  output FeedBack_JMP,
  output Restaura_Buffer_PC
);

  wire Clear, Clock, decoder_1_out1, decoder_1_out2, decoder_1_out3, Out1, Out2;

  Decoder #(.select(2), .enable("false")) decoder_1 (
    .out1(decoder_1_out1), .out2(decoder_1_out2), .out3(decoder_1_out3), .sel({Out2, Out1}));  // open: out0
  J_K_Flip_Flop j_k_ff_1 (.J(1'b1), .clk(Clock), .K(1'b1), .Q(Out1), .reset(Clear));  // open: Qn, preset, en
  and and_1 (Clock, Clock_Geral, JMP_Enable);
  J_K_Flip_Flop j_k_ff_2 (.J(Out1), .clk(Clock), .K(Out1), .Q(Out2), .reset(Clear));  // open: Qn, preset, en
  and and_2 (Clear_PC, decoder_1_out1, JMP_Enable);
  and and_3 (Clock_ADD_IR_____PC, decoder_1_out2, JMP_Enable);
  and and_4 (FeedBack_JMP, decoder_1_out3, JMP_Enable);
  Multiplexer #(.enable("false")) multiplexer_1 (
    .in0(FeedBack_JMP), .in1(Clear_manual), .out(Clear), .sel(Clear_manual));

  assign Restaura_Buffer_PC = 1'b0;

  // Other names for the same wires on the sheet: Clear_Automático = FeedBack_JMP
endmodule

module STP (
  input  Clock_Geral,
  input  STP_Enable,
  input  Clear_manual,
  output Clear_PC,
  output Disable_Circuit,
  output FeedBack_STP
);

  wire Clear, Clock, decoder_1_out1, decoder_1_out2, decoder_1_out3, Out1, Out2;

  Decoder #(.select(2), .enable("false")) decoder_1 (
    .out1(decoder_1_out1), .out2(decoder_1_out2), .out3(decoder_1_out3), .sel({Out2, Out1}));  // open: out0
  J_K_Flip_Flop j_k_ff_1 (.J(1'b1), .clk(Clock), .K(1'b1), .Q(Out1), .reset(Clear));  // open: Qn, preset, en
  and and_1 (Clock, Clock_Geral, STP_Enable);
  and and_2 (Clear_PC, decoder_1_out1, STP_Enable);
  and and_3 (Disable_Circuit, decoder_1_out2, STP_Enable);
  and and_4 (FeedBack_STP, decoder_1_out3, STP_Enable);
  J_K_Flip_Flop j_k_ff_2 (.J(Out1), .clk(Clock), .K(Out1), .Q(Out2), .reset(Clear));  // open: Qn, preset, en
  Multiplexer #(.enable("false")) multiplexer_1 (
    .in0(FeedBack_STP), .in1(Clear_manual), .out(Clear), .sel(Clear_manual));

  // Other names for the same wires on the sheet: Clear_Automático = FeedBack_STP
endmodule

module NOP (
  input  Clock_Geral,
  input  NOP_Enable,
  input  Clear_manual,
  output FeedBack_NOP
);

  wire Clear, Clock, Out1;

  and and_1 (FeedBack_NOP, Out1, NOP_Enable);
  J_K_Flip_Flop j_k_ff_1 (.J(1'b1), .clk(Clock), .K(1'b1), .Q(Out1), .reset(Clear));  // open: Qn, preset, en
  and and_2 (Clock, Clock_Geral, NOP_Enable);
  Multiplexer #(.enable("false")) multiplexer_1 (
    .in0(FeedBack_NOP), .in1(Clear_manual), .out(Clear), .sel(Clear_manual));

  // Other names for the same wires on the sheet: Clear_Automático = FeedBack_NOP
endmodule

// ULA Control
module ULA_cmd (
  input  Clock_Geral,
  input  ULA_cmd_Enable,
  input  Clear_manual,
  output Clock_Buffer_PC,
  output Clear_PC,
  output Clock_ADD_IR____PC,
  output Clock_Read_ACC_____ULA,
  output Clock_Read_RAM_____ULA,
  output Clock_ULA_Operation,
  output Clock_Write_ULA_____ACC,
  output Clock_Write_ACC,
  output Clear_PC_2,
  output Restaura_Buffer_PC,
  output Feedback_ULA_cmd
);

  wire and_2_out, and_14_out, Clear, Clock, decoder_1_out1, decoder_1_out2, decoder_1_out3, decoder_1_out4,
       decoder_1_out5, decoder_1_out6, decoder_1_out7, decoder_1_out8, decoder_1_out9, decoder_1_out10,
       decoder_1_out11, Out1, Out2, Out3, Out4;

  J_K_Flip_Flop j_k_ff_1 (.J(1'b1), .clk(Clock), .K(1'b1), .Q(Out1), .reset(Clear));  // open: Qn, preset, en
  and and_1 (Clock, Clock_Geral, ULA_cmd_Enable);
  Decoder #(.select(4), .enable("false")) decoder_1 (
    .out1(decoder_1_out1), .out2(decoder_1_out2), .out3(decoder_1_out3), .out4(decoder_1_out4),
    .out5(decoder_1_out5), .out6(decoder_1_out6), .out7(decoder_1_out7), .out8(decoder_1_out8),
    .out9(decoder_1_out9), .out10(decoder_1_out10), .out11(decoder_1_out11), .sel({Out4, Out3, Out2, Out1}));  // open: out0, out12, out13, out14, out15
  J_K_Flip_Flop j_k_ff_2 (.J(Out1), .clk(Clock), .K(Out1), .Q(Out2), .reset(Clear));  // open: Qn, preset, en
  and and_2 (and_2_out, Out1, Out2);
  J_K_Flip_Flop j_k_ff_3 (.J(and_2_out), .clk(Clock), .K(and_2_out), .Q(Out3), .reset(Clear));  // open: Qn, preset, en
  and and_3 (Clock_Buffer_PC, decoder_1_out1, ULA_cmd_Enable);
  and and_4 (Clear_PC, decoder_1_out2, ULA_cmd_Enable);
  and and_5 (Clock_ADD_IR____PC, decoder_1_out3, ULA_cmd_Enable);
  and and_6 (Clock_Read_ACC_____ULA, decoder_1_out4, ULA_cmd_Enable);
  and and_7 (Clock_Read_RAM_____ULA, decoder_1_out5, ULA_cmd_Enable);
  and and_8 (Clock_ULA_Operation, decoder_1_out6, ULA_cmd_Enable);
  and and_9 (Clock_Write_ULA_____ACC, decoder_1_out7, ULA_cmd_Enable);
  and and_10 (Clock_Write_ACC, decoder_1_out8, ULA_cmd_Enable);
  and and_11 (Clear_PC_2, decoder_1_out9, ULA_cmd_Enable);
  and and_12 (Restaura_Buffer_PC, decoder_1_out10, ULA_cmd_Enable);
  and and_13 (Feedback_ULA_cmd, decoder_1_out11, ULA_cmd_Enable);
  and and_14 (and_14_out, and_2_out, Out3);
  J_K_Flip_Flop j_k_ff_4 (
    .J(and_14_out), .clk(Clock), .K(and_14_out), .Q(Out4), .reset(Clear));  // open: Qn, preset, en
  Multiplexer #(.enable("false")) multiplexer_1 (
    .in0(Feedback_ULA_cmd), .in1(Clear_manual), .out(Clear), .sel(Clear_manual));

  // Other names for the same wires on the sheet: Clear_Automático = Feedback_ULA_cmd
endmodule

module Command (
  input  [7:0] Instruction,
  input  Clock_Instruction,
  output LDA,
  output ADD,
  output JLE,
  output IN,
  output STA,
  output SUB,
  output JDZ,
  output PRN,
  output NOP,
  output MUL,
  output JGT,
  output JMP,
  output DIV,
  output JEQ,
  output STP,
  output REM,
  output JLT,
  output JGE
);

  wire not_1_out;
  wire [7:0] Instruction_t;

  Comparator comparator_1 (.a(8'hb), .b(Instruction_t), .eq(LDA));  // open: gt, lt
  Comparator comparator_2 (.a(8'hc), .b(Instruction_t), .eq(STA));  // open: gt, lt
  Comparator comparator_3 (.a(8'h32), .b(Instruction_t), .eq(NOP));  // open: gt, lt
  Comparator comparator_4 (.a(8'h33), .b(Instruction_t), .eq(JMP));  // open: gt, lt
  Comparator comparator_5 (.a(8'h70), .b(Instruction_t), .eq(STP));  // open: gt, lt
  Comparator comparator_6 (.a(8'h15), .b(Instruction_t), .eq(ADD));  // open: gt, lt
  Comparator comparator_7 (.a(8'h16), .b(Instruction_t), .eq(SUB));  // open: gt, lt
  Comparator comparator_8 (.a(8'h17), .b(Instruction_t), .eq(MUL));  // open: gt, lt
  Comparator comparator_9 (.a(8'h18), .b(Instruction_t), .eq(DIV));  // open: gt, lt
  Comparator comparator_10 (.a(8'h19), .b(Instruction_t), .eq(REM));  // open: gt, lt
  Multiplexer #(.width(8)) multiplexer_1 (
    .in0(Instruction), .in1({8{1'b0}}), .out(Instruction_t), .sel(not_1_out));  // open: en
  not not_1 (not_1_out, Clock_Instruction);
  Comparator comparator_11 (.a(8'h34), .b(Instruction_t), .eq(JLE));  // open: gt, lt
  Comparator comparator_12 (.a(8'h35), .b(Instruction_t), .eq(JDZ));  // open: gt, lt
  Comparator comparator_13 (.a(8'h36), .b(Instruction_t), .eq(JGT));  // open: gt, lt
  Comparator comparator_14 (.a(8'h37), .b(Instruction_t), .eq(JEQ));  // open: gt, lt
  Comparator comparator_15 (.a(8'h38), .b(Instruction_t), .eq(JLT));  // open: gt, lt
  Comparator comparator_16 (.a(8'h39), .b(Instruction_t), .eq(JGE));  // open: gt, lt
  Comparator comparator_17 (.a(8'h1f), .b(Instruction_t), .eq(IN));  // open: gt, lt
  Comparator comparator_18 (.a(8'h29), .b(Instruction_t), .eq(PRN));  // open: gt, lt

  // Notes on the sheet:
  //   Manipulação da memória
  //   Aritmética
  //   Saltos Condicionais
  //   Entrada/Saída de Dados
endmodule

module FDX_Init (
  input  Clock_Geral,
  input  Clear_FDX,
  output Clock_IR,
  output Clock_PC,
  output Clock_Command
);

  wire Out1, Out2;

  J_K_Flip_Flop j_k_ff_1 (.J(1'b1), .clk(Clock_Geral), .K(1'b1), .Q(Out1), .reset(Clear_FDX));  // open: Qn, preset, en
  J_K_Flip_Flop j_k_ff_2 (.J(Out1), .clk(Clock_Geral), .K(Out1), .Q(Out2), .reset(Clear_FDX));  // open: Qn, preset, en
  Decoder #(.select(2), .enable("false")) decoder_1 (
    .out1(Clock_IR), .out2(Clock_PC), .out3(Clock_Command), .sel({Out2, Out1}));  // open: out0

  // Other names for the same wires on the sheet: Clear = Clear_FDX; Clock = Clock_Geral
endmodule

// Power
module Power_Circuit (
  input  Forced_Reset,
  input  Overflow_In,
  input  Zero_division_In,
  input  Power_On,
  input  Clock_Principal,
  input  Disable_Option,
  output Zero_division_Out,
  output Overflow_Out,
  output Clock_Principal_2,
  output Estado_do_Circuito
);

  wire or_1_out, Stop_Execution;

  J_K_Flip_Flop j_k_ff_1 (
    .J(1'b1), .clk(Power_On), .K(1'b1), .Q(Estado_do_Circuito), .reset(or_1_out));  // open: Qn, preset, en
  or or_1 (or_1_out, Stop_Execution, Forced_Reset);
  J_K_Flip_Flop j_k_ff_2 (
    .J(1'b1), .clk(Overflow_In), .K(1'b1), .Q(Overflow_Out), .reset(Forced_Reset));  // open: Qn, preset, en
  or or_2 (Stop_Execution, Disable_Option, Overflow_In, Zero_division_In);
  J_K_Flip_Flop j_k_ff_3 (
    .J(1'b1), .clk(Zero_division_In), .K(1'b1), .Q(Zero_division_Out), .reset(Forced_Reset));  // open: Qn, preset, en
  Multiplexer #(.enable("false")) multiplexer_1 (
    .in0(1'b0), .in1(Clock_Principal), .out(Clock_Principal_2), .sel(Estado_do_Circuito));

  // Other names for the same wires on the sheet: Out1 = Estado_do_Circuito; Overflow = Overflow_In;
  //   Zero_Division = Zero_division_In
endmodule

module CMD2 (
  input  [7:0] Instruction,
  input  Clock_Instruction,
  output LDA,
  output ADD,
  output JLE,
  output IN,
  output STA,
  output SUB,
  output JDZ,
  output PRN,
  output NOP,
  output MUL,
  output JGT,
  output JMP,
  output DIV,
  output JEQ,
  output STP,
  output REM,
  output JLT,
  output JGE
);

  wire not_1_out;
  wire [7:0] Instruction_t;

  Comparator comparator_1 (.a(8'hb), .b(Instruction_t), .eq(LDA));  // open: gt, lt
  Comparator comparator_2 (.a(8'hc), .b(Instruction_t), .eq(STA));  // open: gt, lt
  Comparator comparator_3 (.a(8'h32), .b(Instruction_t), .eq(NOP));  // open: gt, lt
  Comparator comparator_4 (.a(8'h33), .b(Instruction_t), .eq(JMP));  // open: gt, lt
  Comparator comparator_5 (.a(8'h70), .b(Instruction_t), .eq(STP));  // open: gt, lt
  Comparator comparator_6 (.a(8'h15), .b(Instruction_t), .eq(ADD));  // open: gt, lt
  Comparator comparator_7 (.a(8'h16), .b(Instruction_t), .eq(SUB));  // open: gt, lt
  Comparator comparator_8 (.a(8'h17), .b(Instruction_t), .eq(MUL));  // open: gt, lt
  Comparator comparator_9 (.a(8'h18), .b(Instruction_t), .eq(DIV));  // open: gt, lt
  Comparator comparator_10 (.a(8'h19), .b(Instruction_t), .eq(REM));  // open: gt, lt
  not not_1 (not_1_out, Clock_Instruction);
  Multiplexer #(.width(8)) multiplexer_1 (
    .in0(Instruction), .in1({8{1'b0}}), .out(Instruction_t), .sel(not_1_out));  // open: en
  Comparator comparator_11 (.a(8'h34), .b(Instruction_t), .eq(JLE));  // open: gt, lt
  Comparator comparator_12 (.a(8'h35), .b(Instruction_t), .eq(JDZ));  // open: gt, lt
  Comparator comparator_13 (.a(8'h36), .b(Instruction_t), .eq(JGT));  // open: gt, lt
  Comparator comparator_14 (.a(8'h37), .b(Instruction_t), .eq(JEQ));  // open: gt, lt
  Comparator comparator_15 (.a(8'h38), .b(Instruction_t), .eq(JLT));  // open: gt, lt
  Comparator comparator_16 (.a(8'h39), .b(Instruction_t), .eq(JGE));  // open: gt, lt
  Comparator comparator_17 (.a(8'h1f), .b(Instruction_t), .eq(IN));  // open: gt, lt
  Comparator comparator_18 (.a(8'h29), .b(Instruction_t), .eq(PRN));  // open: gt, lt

  // Notes on the sheet:
  //   Manipulação da memória
  //   Aritmética
  //   Saltos Condicionais
  //   Entrada/Saída de Dados
endmodule

module ULA (
  input  [15:0] ACC____ULA,
  input  [15:0] RAM____ULA,
  input  Clock_Geral,
  input  [8:0] ULA_Binary_Code_IN,
  input  clear,
  output [15:0] ULA____ACC,
  output overflow,
  output div_0,
  output Conditional_Jump
);

  wire [15:0] A, B;

  Register #(.width(16)) Acumulador (.D(ACC____ULA), .en(1'b1), .Q(A), .clk(ULA_Binary_Code_IN[0]), .clr(clear));
  Register #(.width(16)) Acumulador_2 (.D(RAM____ULA), .en(1'b1), .Q(B), .clk(ULA_Binary_Code_IN[0]), .clr(clear));
  ULA_Circuit ula_circuit_1 (
    .A(A), .B(B), .Operation(ULA_Binary_Code_IN[8:4]), .Set_Operation(ULA_Binary_Code_IN[2]),
    .Set_NULL_Operation(ULA_Binary_Code_IN[3]), .Result(ULA____ACC), .Overflow(overflow),
    .Zero_division(div_0), .Cond_Jump(Conditional_Jump));

  // Other names for the same wires on the sheet: Clear_Manual = clear; Clock_Read_ACC_____ULA = ULA_Binary_Code_IN[0];
  //   Clock_Read_RAM____ULA = ULA_Binary_Code_IN[1]; Clock_ULA_Operation = ULA_Binary_Code_IN[2];
  //   NULL_Operation = ULA_Binary_Code_IN[3]; Operation[4:0] = ULA_Binary_Code_IN[8:4]
endmodule

module ULA_Circuit (
  input  [15:0] A,
  input  [15:0] B,
  input  [4:0] Operation,
  input  Set_Operation,
  input  Set_NULL_Operation,
  output [15:0] Result,
  output Overflow,
  output Zero_division,
  output Cond_Jump
);

  wire [4:0] register_1_q;
  wire [15:0] ADD, DIV, MUL, REM, SUB;

  Register #(.width(5)) register_1 (
    .D(Operation), .Q(register_1_q), .clk(Set_Operation), .clr(Set_NULL_Operation));  // open: en
  Multiplexer #(.select(5), .width(16)) multiplexer_1 (
    .in0({16{1'b0}}), .in1(ADD), .in2(SUB), .in4(MUL), .in8(DIV), .in16(REM), .out(Result), .sel(register_1_q));  // open: in3, in5, in6, in7, in9, in10, in11, in12, in13, in14, in15, in17, in18, in19, in20, in21, in22, in23, in24, in25, in26, in27, in28, in29, in30, in31, en
  Adder #(.width(16)) adder_1 (.a(A), .b(B), .out(ADD));  // open: cin, cout

  // Other names for the same wires on the sheet: Conditional_Jump = Cond_Jump; Resultado[15:0] = Result

  // Notes on the sheet:
  //   Exemplo de como funcionaria a soma
endmodule
