// Logisim project Adder-Subtractor.circ as structural Verilog: 4 circuits, main circuit Adder/Subtractor
module Adder_Subtractor (
  input  [7:0] a,
  input  [7:0] b,
  input  OP_Code,
  output [7:0] Result,
  output Overflow
);

  wire [7:0] multiplexer_1_out, twos_complement_1_twos_complement_of_a;

  Multiplexer #(.width(8)) multiplexer_1 (
    .in0(b), .in1(twos_complement_1_twos_complement_of_a), .out(multiplexer_1_out), .sel(OP_Code), .en(1'b1));
  Twos_Complement twos_complement_1 (.a(b), .twos_complement_of_a(twos_complement_1_twos_complement_of_a));
  _8_bit_Riple_Carry_Adder u_8_bit_riple_carry_adder_1 (
    .a(a), .b(multiplexer_1_out), .Result(Result), .Overflow(Overflow));

  // Notes on the sheet:
  //   0: Sum, 1: Subtraction
endmodule

module Twos_Complement (
  input  [7:0] a,
  output [7:0] twos_complement_of_a
);

  wire [7:0] not_1_out;

  assign not_1_out = ~a;  // NOT_Gate not_1, 8 bits wide
  _8_bit_Riple_Carry_Adder u_8_bit_riple_carry_adder_1 (
    .a(not_1_out), .b(8'h1), .Result(twos_complement_of_a));  // open: Overflow
endmodule

module _8_bit_Riple_Carry_Adder (
  input  [7:0] a,
  input  [7:0] b,
  output [7:0] Result,
  output Overflow
);

  wire full_adder_1_carry, full_adder_2_carry, full_adder_3_carry, full_adder_4_carry, full_adder_5_carry,
       full_adder_6_carry, full_adder_7_carry, full_adder_8_carry, xnor_1_out, xor_1_out;

  Full_Adder full_adder_1 (.a(a[7]), .b(b[7]), .c(full_adder_2_carry), .Sum(Result[7]), .Carry(full_adder_1_carry));
  Full_Adder full_adder_2 (.a(a[6]), .b(b[6]), .c(full_adder_3_carry), .Sum(Result[6]), .Carry(full_adder_2_carry));
  xor xor_1 (xor_1_out, Result[7], b[7]);
  xnor xnor_1 (xnor_1_out, b[7], a[7]);
  Full_Adder full_adder_3 (.a(a[5]), .b(b[5]), .c(full_adder_5_carry), .Sum(Result[5]), .Carry(full_adder_3_carry));
  and and_1 (Overflow, xor_1_out, xnor_1_out);
  Full_Adder full_adder_4 (.a(a[3]), .b(b[3]), .c(full_adder_6_carry), .Sum(Result[3]), .Carry(full_adder_4_carry));
  Full_Adder full_adder_5 (.a(a[4]), .b(b[4]), .c(full_adder_4_carry), .Sum(Result[4]), .Carry(full_adder_5_carry));
  Full_Adder full_adder_6 (.a(a[2]), .b(b[2]), .c(full_adder_7_carry), .Sum(Result[2]), .Carry(full_adder_6_carry));
  Full_Adder full_adder_7 (.a(a[1]), .b(b[1]), .c(full_adder_8_carry), .Sum(Result[1]), .Carry(full_adder_7_carry));
  Full_Adder full_adder_8 (.a(a[0]), .b(b[0]), .c(1'b0), .Sum(Result[0]), .Carry(full_adder_8_carry));

  // Notes on the sheet:
  //   Overflow occurs if and only if sign(a) = sign(b) and it is different from sign(c)
endmodule

module Full_Adder (
  input  a,
  input  b,
  input  c,
  output Sum,
  output Carry
);

  wire and_1_out, and_2_out, and_3_out, xor_1_out;

  xor xor_1 (xor_1_out, a, b);
  and and_1 (and_1_out, a, b);
  or or_1 (Carry, and_1_out, and_2_out, and_3_out);
  and and_2 (and_2_out, a, c);
  and and_3 (and_3_out, b, c);
  xor xor_2 (Sum, xor_1_out, c);
endmodule
