// Logisim project full_adder_somente_nand_com_visualizacao.circ as structural Verilog: 4 circuits, main circuit Half Adder
module Visualization (
  input  in_1,
  input  in_2,
  input  in_3,
  input  in_4,
  input  in_5,
  input  in_6,
  input  in_7,
  input  in_8,
  input  in_9,
  input  in_10,
  input  in_11,
  input  in_12,
  input  in_13,
  input  in_14,
  input  in_15,
  input  in_16,
  input  in_17
);

  wire n8_bit_full_adder_1_overflow;
  wire [3:0] n8_bit_full_adder_1_r0, n8_bit_full_adder_1_r4;

  Hex_Digit_Display hex_digit_display_1 (.value({in_5, in_6, in_7, in_8}));  // open: dp
  Hex_Digit_Display hex_digit_display_2 (.value({in_1, in_2, in_3, in_4}));  // open: dp
  LED Overflow (.in(n8_bit_full_adder_1_overflow));
  Hex_Digit_Display hex_digit_display_3 (.value(n8_bit_full_adder_1_r4));  // open: dp
  _8_bit_Full_Adder u_8_bit_full_adder_1 (
    .b7(in_1), .b6(in_2), .b5(in_3), .b4(in_4), .b3(in_5), .b2(in_6), .b1(in_7), .b0(in_8), .a7(in_9),
    .a6(in_10), .a5(in_11), .a4(in_12), .a3(in_13), .a2(in_14), .a1(in_15), .a0(in_16),
    .overflow(n8_bit_full_adder_1_overflow), .r7(n8_bit_full_adder_1_r4[3]), .r6(n8_bit_full_adder_1_r4[2]),
    .r5(n8_bit_full_adder_1_r4[1]), .r4(n8_bit_full_adder_1_r4[0]), .r3(n8_bit_full_adder_1_r0[3]),
    .r2(n8_bit_full_adder_1_r0[2]), .r1(n8_bit_full_adder_1_r0[1]), .r0(n8_bit_full_adder_1_r0[0]),
    .Carry_Inicial(in_17));
  Hex_Digit_Display hex_digit_display_4 (.value(n8_bit_full_adder_1_r0));  // open: dp
  Hex_Digit_Display hex_digit_display_5 (.value({in_13, in_14, in_15, in_16}));  // open: dp
  Hex_Digit_Display hex_digit_display_6 (.value({in_9, in_10, in_11, in_12}));  // open: dp

  // Notes on the sheet:
  //   a
  //   8-bit Adder - Hexadecimal Representation
  //   a+b
  //   b
endmodule

module _8_bit_Full_Adder (
  input  b7,
  input  b6,
  input  b5,
  input  b4,
  input  b3,
  input  b2,
  input  b1,
  input  b0,
  input  a7,
  input  a6,
  input  a5,
  input  a4,
  input  a3,
  input  a2,
  input  a1,
  input  a0,
  input  Carry_Inicial,
  output overflow,
  output r7,
  output r6,
  output r5,
  output r4,
  output r3,
  output r2,
  output r1,
  output r0
);

  wire full_adder_2_carry_bit, full_adder_3_carry_bit, full_adder_4_carry_bit, full_adder_5_carry_bit,
       full_adder_6_carry_bit, full_adder_7_carry_bit, full_adder_8_carry_bit;

  Full_Adder full_adder_1 (.a(a7), .b(b7), .c__carry(full_adder_2_carry_bit), .Carry_Bit(overflow), .Answer_Bit(r7));
  Full_Adder full_adder_2 (
    .a(a6), .b(b6), .c__carry(full_adder_3_carry_bit), .Carry_Bit(full_adder_2_carry_bit), .Answer_Bit(r6));
  Full_Adder full_adder_3 (
    .a(a5), .b(b5), .c__carry(full_adder_4_carry_bit), .Carry_Bit(full_adder_3_carry_bit), .Answer_Bit(r5));
  Full_Adder full_adder_4 (
    .a(a4), .b(b4), .c__carry(full_adder_5_carry_bit), .Carry_Bit(full_adder_4_carry_bit), .Answer_Bit(r4));
  Full_Adder full_adder_5 (
    .a(a3), .b(b3), .c__carry(full_adder_6_carry_bit), .Carry_Bit(full_adder_5_carry_bit), .Answer_Bit(r3));
  Full_Adder full_adder_6 (
    .a(a2), .b(b2), .c__carry(full_adder_7_carry_bit), .Carry_Bit(full_adder_6_carry_bit), .Answer_Bit(r2));
  Full_Adder full_adder_7 (
    .a(a1), .b(b1), .c__carry(full_adder_8_carry_bit), .Carry_Bit(full_adder_7_carry_bit), .Answer_Bit(r1));
  Full_Adder full_adder_8 (
    .a(a0), .b(b0), .c__carry(Carry_Inicial), .Carry_Bit(full_adder_8_carry_bit), .Answer_Bit(r0));
endmodule

module Full_Adder (
  input  a,
  input  b,
  input  c__carry,
  output Carry_Bit,
  output Answer_Bit
);

  wire half_adder_1_carry_over_bit, half_adder_1_sum_bit, half_adder_2_carry_over_bit, nand_1_out, nand_2_out;

  Half_Adder half_adder_1 (.a(a), .b(b), .Carry_Over_Bit(half_adder_1_carry_over_bit), .Sum_Bit(half_adder_1_sum_bit));
  Half_Adder half_adder_2 (
    .a(half_adder_1_sum_bit), .b(c__carry), .Carry_Over_Bit(half_adder_2_carry_over_bit), .Sum_Bit(Answer_Bit));
  nand nand_1 (nand_1_out, half_adder_1_carry_over_bit, half_adder_1_carry_over_bit);
  nand nand_2 (nand_2_out, half_adder_2_carry_over_bit, half_adder_2_carry_over_bit);
  nand nand_3 (Carry_Bit, nand_1_out, nand_2_out);
endmodule

module Half_Adder (
  input  a,
  input  b,
  output Carry_Over_Bit,
  output Sum_Bit
);

  wire nand_1_out, nand_2_out, nand_3_out, nand_5_out, nand_6_out;

  nand nand_1 (nand_1_out, a, b);
  nand nand_2 (nand_2_out, a, a);
  nand nand_3 (nand_3_out, b, b);
  nand nand_4 (Carry_Over_Bit, nand_1_out, nand_1_out);
  nand nand_5 (nand_5_out, nand_2_out, b);
  nand nand_6 (nand_6_out, a, nand_3_out);
  nand nand_7 (Sum_Bit, nand_5_out, nand_6_out);

  // Notes on the sheet:
  //   a
  //   b
  //   a
  //   b
  //   a NAND b
  //   ~a
  //   Half Adder using only NAND gates
  //   b
  //   a
  //   ~b
  //   a AND b
  //   a XOR b
endmodule
