// Logisim project half_adder_somente_nand.circ as structural Verilog: 1 circuit, main circuit Half Adder
module Half_Adder (
  input  a,
  input  b
);

  wire nand_1_out, nand_2_out, nand_3_out, nand_4_out, nand_5_out, nand_6_out, nand_7_out;

  nand nand_1 (nand_1_out, a, b);
  nand nand_2 (nand_2_out, a, a);
  nand nand_3 (nand_3_out, b, b);
  nand nand_4 (nand_4_out, nand_1_out, nand_1_out);
  nand nand_5 (nand_5_out, nand_2_out, b);
  nand nand_6 (nand_6_out, a, nand_3_out);
  nand nand_7 (nand_7_out, nand_5_out, nand_6_out);
  LED led_1 (.in(nand_4_out));
  LED led_2 (.in(nand_7_out));

  // Notes on the sheet:
  //   a
  //   b
  //   a
  //   b
  //   a NAND b
  //   ~a
  //   Half Adder using only NAND gates
  //   b
  //   a
  //   ~b
  //   a AND b
  //   a XOR b
  //   Sum bit
  //   Carry over bit
endmodule
