// Logisim project half_adder_varios_jeitos.circ as structural Verilog: 1 circuit, main circuit Half Adder
module Half_Adder (
  input  a,
  input  b
);

  wire and_1_out, and_2_out, nand_1_out, nand_2_out, nand_3_out, nand_4_out, nand_5_out, nand_6_out,
       nand_7_out, not_1_out, or_1_out, xor_1_out;

  nand nand_1 (nand_1_out, a, b);
  and and_1 (and_1_out, a, b);
  not not_1 (not_1_out, and_1_out);
  or or_1 (or_1_out, a, b);
  xor xor_1 (xor_1_out, a, b);
  nand nand_2 (nand_2_out, a, a);
  nand nand_3 (nand_3_out, b, b);
  nand nand_4 (nand_4_out, nand_1_out, nand_1_out);
  and and_2 (and_2_out, not_1_out, or_1_out);
  nand nand_5 (nand_5_out, nand_2_out, b);
  nand nand_6 (nand_6_out, a, nand_3_out);
  nand nand_7 (nand_7_out, nand_5_out, nand_6_out);
  LED led_1 (.in(nand_4_out));
  LED led_2 (.in(and_1_out));
  LED led_3 (.in(and_2_out));
  LED led_4 (.in(xor_1_out));
  LED led_5 (.in(nand_7_out));

  // Notes on the sheet:
  //   a
  //   b
  //   a NAND b
  //   a AND b
  //   a OR b
  //   a NAND b
  //   ~a
  //   b
  //   a
  //   ~b
  //   (a NAND b) NAND (a NAND b) = a AND b
  //   a XOR b
  //   (NOT (a AND b)) AND (a OR B) = a XOR b
  //   Carry over bit
  //   (~a^b) OR (a^~b) = a XOR b
  //   Using only NAND
  //   Sum bit
  //   Using only AND (for demonstration)
  //   Using 4 gates
  //   Using only XOR (for demonstration)
  //   Using only NAND
endmodule
