// Logisim project alu.circ as structural Verilog: 2 circuits, main circuit main
module main (
  input  in_1,
  input  in_2,
  input  in_3,
  input  in_4,
  input  in_5,
  input  in_6,
  input  in_7,
  input  in_8,
  input  in_9,
  input  in_10,
  input  in_11,
  input  in_12,
  input  in_13,
  input  in_14,
  input  in_15,
  input  in_16
);

  ALU alu_1 ();  // open: a0, a1, a2, a3, a4, a5, a6, a7, b0, b1, b2, b3, b4, b5, b6, b7, s0, s1, s2, r0, r1, r2, r3, r4, r5, r6, r7, overflow
endmodule

module ALU (
  input  a0,
  input  a1,
  input  a2,
  input  a3,
  input  a4,
  input  a5,
  input  a6,
  input  a7,
  input  b0,
  input  b1,
  input  b2,
  input  b3,
  input  b4,
  input  b5,
  input  b6,
  input  b7,
  input  s0,
  input  s1,
  input  s2,
  output r0,
  output r1,
  output r2,
  output r3,
  output r4,
  output r5,
  output r6,
  output r7,
  output overflow
);

  Adder adder_1 (
    .a({a7, a6, a5, a4, a3, a2, a1, a0}), .b({b7, b6, b5, b4, b3, b2, b1, b0}),
    .out({r7, r6, r5, r4, r3, r2, r1, r0}), .cout(overflow));  // open: cin
endmodule
